// Logisim project S-ADD_d.circ as structural Verilog
module S_ADD (
  input  \х1 ,
  input  \х2 ,
  output \Младший ,
  output \Смещение 
);

  xor xor_1 (\Младший , \х1 , \х2 );
  and and_1 (\Смещение , \х1 , \х2 );
endmodule

module ADD1 (
  input  in_1,
  input  \х1 ,
  input  \х2 ,
  output \Значащий ,
  output \Смещение 
);

  wire and_1_out, \s_add_1_младший , \s_add_1_смещение ;

  S_ADD s_add_1 (.\х1 (\х1 ), .\х2 (\х2 ), .\Младший (\s_add_1_младший ), .\Смещение (\s_add_1_смещение ));
  xor xor_1 (\Значащий , in_1, \s_add_1_младший );
  and and_1 (and_1_out, in_1, \s_add_1_младший );
  or or_1 (\Смещение , and_1_out, \s_add_1_смещение );
endmodule

module ADD8u (
  input  [7:0] in_1,
  input  [7:0] in_2,
  output [7:0] out_3,
  output out_4,
  output out_5
);

  wire \add1_1_смещение , \add1_2_смещение , \add1_3_смещение , \add1_4_смещение , \add1_5_смещение ,
       \s_add_1_смещение ;

  S_ADD s_add_1 (.\х1 (in_1[0]), .\х2 (in_2[0]), .\Младший (out_3[0]), .\Смещение (\s_add_1_смещение ));
  ADD1 add1_1 (
    .in_1(\s_add_1_смещение ), .\х1 (in_1[1]), .\х2 (in_2[1]), .\Значащий (out_3[1]),
    .\Смещение (\add1_1_смещение ));
  ADD1 add1_2 (
    .in_1(\add1_1_смещение ), .\х1 (in_1[2]), .\х2 (in_2[2]), .\Значащий (out_3[2]),
    .\Смещение (\add1_2_смещение ));
  ADD1 add1_3 (
    .in_1(\add1_2_смещение ), .\х1 (in_1[3]), .\х2 (in_2[3]), .\Значащий (out_3[3]),
    .\Смещение (\add1_3_смещение ));
  ADD1 add1_4 (
    .in_1(\add1_3_смещение ), .\х1 (in_1[4]), .\х2 (in_2[4]), .\Значащий (out_3[4]),
    .\Смещение (\add1_4_смещение ));
  ADD1 add1_5 (
    .in_1(\add1_4_смещение ), .\х1 (in_1[5]), .\х2 (in_2[5]), .\Значащий (out_3[5]),
    .\Смещение (\add1_5_смещение ));
  ADD1 add1_6 (.in_1(\add1_5_смещение ), .\х1 (in_1[6]), .\х2 (in_2[6]), .\Значащий (out_3[6]), .\Смещение (out_4));
  ADD1 add1_7 (.in_1(out_4), .\х1 (in_1[7]), .\х2 (in_2[7]), .\Значащий (out_3[7]), .\Смещение (out_5));
endmodule

module Multiplexor2 (
  input  in_1,
  input  in_2,
  input  in_3,
  output out_4
);

  wire and_1_out, and_2_out, not_1_out;

  not not_1 (not_1_out, in_3);
  and and_1 (and_1_out, in_1, not_1_out);
  and and_2 (and_2_out, in_2, in_3);
  or or_1 (out_4, and_1_out, and_2_out);
endmodule

module ALU (
  input  [3:0] in_1,
  input  [7:0] In1,
  input  [7:0] In2,
  input  Sign,
  input  [2:0] in_5,
  output [7:0] out_6
);

  wire [7:0] adder_1_out, demultiplexer_1_out0, demultiplexer_1_out1, demultiplexer_1_out2,
       demultiplexer_1_out3, demultiplexer_1_out4, demultiplexer_1_out5, demultiplexer_1_out6,
       demultiplexer_1_out7, demultiplexer_1_out8, demultiplexer_1_out9, demultiplexer_2_out0,
       demultiplexer_2_out1, demultiplexer_2_out2, demultiplexer_2_out3, demultiplexer_2_out4, divider_1_out,
       multiplier_1_out, shifter_1_out, shifter_2_out, shifter_3_out, shifter_4_out, shifter_5_out,
       subtractor_1_out;

  Demultiplexer #(.select(4), .width(8), .enable("false")) demultiplexer_1 (
    .out0(demultiplexer_1_out0), .out1(demultiplexer_1_out1), .out2(demultiplexer_1_out2),
    .out3(demultiplexer_1_out3), .out4(demultiplexer_1_out4), .out5(demultiplexer_1_out5),
    .out6(demultiplexer_1_out6), .out7(demultiplexer_1_out7), .out8(demultiplexer_1_out8),
    .out9(demultiplexer_1_out9), .in(In1), .sel(in_1));  // open: out10, out11, out12, out13, out14, out15
  Demultiplexer #(.select(4), .width(8), .enable("false")) demultiplexer_2 (
    .out0(demultiplexer_2_out0), .out1(demultiplexer_2_out1), .out2(demultiplexer_2_out2),
    .out3(demultiplexer_2_out3), .out4(demultiplexer_2_out4), .sel(in_1));  // open: out5, out6, out7, out8, out9, out10, out11, out12, out13, out14, out15, in
  Adder adder_1 (.a(demultiplexer_1_out0), .b(demultiplexer_2_out0), .out(adder_1_out));  // open: cin, cout
  Subtractor subtractor_1 (
    .a(demultiplexer_1_out1), .b(demultiplexer_2_out1), .out(subtractor_1_out));  // open: bin, bout
  Multiplier multiplier_1 (
    .a(demultiplexer_1_out2), .b(demultiplexer_2_out2), .out(multiplier_1_out));  // open: cin, cout
  Divider divider_1 (.a(demultiplexer_1_out3), .b(demultiplexer_2_out3), .out(divider_1_out));  // open: upper, rem
  Shifter shifter_1 (.in(demultiplexer_1_out9), .\dist (in_5), .out(shifter_1_out));
  Shifter #(.shift("lr")) shifter_2 (.in(demultiplexer_1_out5), .\dist (in_5), .out(shifter_2_out));
  Shifter #(.shift("ar")) shifter_3 (.in(demultiplexer_1_out6), .\dist (in_5), .out(shifter_3_out));
  Shifter #(.shift("rl")) shifter_4 (.in(demultiplexer_1_out7), .\dist (in_5), .out(shifter_4_out));
  Shifter #(.shift("rl")) shifter_5 (.in(demultiplexer_1_out8), .\dist (in_5), .out(shifter_5_out));
  Comp8u comp8u_1 (
    .in_1(demultiplexer_2_out4), .in_2(demultiplexer_1_out4), .in_3(Sign));  // open: A____B, A___B, A____B_2, A___B_2, A___B_3, A____B_3
  Multiplexer #(.select(4), .width(8), .disabled(0), .enable("false")) multiplexer_1 (
    .in0(adder_1_out), .in1(subtractor_1_out), .in2(multiplier_1_out), .in3(divider_1_out),
    .in4(shifter_1_out), .in5(shifter_2_out), .in6(shifter_3_out), .in7(shifter_4_out), .in8(shifter_5_out),
    .out(out_6), .sel(in_1));  // open: in9, in10, in11, in12, in13, in14, in15
endmodule

module Multiply8x8u (
  input  [7:0] in_1,
  input  [7:0] in_2,
  output [7:0] out_3
);

  wire [7:0] add8u_1_out_3, add8u_2_out_3, add8u_3_out_3, add8u_4_out_3, add8u_5_out_3, add8u_6_out_3,
       multiply8x1u_1_out_3, multiply8x1u_2_out_3, multiply8x1u_3_out_3, multiply8x1u_4_out_3,
       multiply8x1u_5_out_3, multiply8x1u_6_out_3, multiply8x1u_7_out_3, multiply8x1u_8_out_3,
       sl_r_l_1_1_out_3, sl_r_l_1_2_out_3, sl_r_l_1_3_out_3, sl_r_l_1_4_out_3, sl_r_l_1_5_out_3,
       sl_r_l_1_6_out_3, sl_r_l_1_7_out_3;

  Multiply8x1u multiply8x1u_1 (.in_1(in_2[0]), .in_2(in_1), .out_3(multiply8x1u_1_out_3));
  Multiply8x1u multiply8x1u_2 (.in_1(in_2[1]), .in_2(in_1), .out_3(multiply8x1u_2_out_3));
  Multiply8x1u multiply8x1u_3 (.in_1(in_2[2]), .in_2(in_1), .out_3(multiply8x1u_3_out_3));
  Multiply8x1u multiply8x1u_4 (.in_1(in_2[3]), .in_2(in_1), .out_3(multiply8x1u_4_out_3));
  Multiply8x1u multiply8x1u_5 (.in_1(in_2[4]), .in_2(in_1), .out_3(multiply8x1u_5_out_3));
  Multiply8x1u multiply8x1u_6 (.in_1(in_2[5]), .in_2(in_1), .out_3(multiply8x1u_6_out_3));
  Multiply8x1u multiply8x1u_7 (.in_1(in_2[6]), .in_2(in_1), .out_3(multiply8x1u_7_out_3));
  Multiply8x1u multiply8x1u_8 (.in_1(in_2[7]), .in_2(in_1), .out_3(multiply8x1u_8_out_3));
  SL_R_L_1 sl_r_l_1_1 (.in_1(multiply8x1u_2_out_3), .in_2(1'b0), .out_3(sl_r_l_1_1_out_3));
  ADD8u add8u_1 (.in_1(multiply8x1u_1_out_3), .in_2(sl_r_l_1_1_out_3), .out_3(add8u_1_out_3));  // open: out_4, out_5
  SL_R_L_1 sl_r_l_1_2 (.in_1(multiply8x1u_3_out_3), .in_2(1'b0), .out_3(sl_r_l_1_2_out_3));
  ADD8u add8u_2 (.in_1(add8u_1_out_3), .in_2(sl_r_l_1_2_out_3), .out_3(add8u_2_out_3));  // open: out_4, out_5
  SL_R_L_1 sl_r_l_1_3 (.in_1(multiply8x1u_4_out_3), .in_2(1'b0), .out_3(sl_r_l_1_3_out_3));
  ADD8u add8u_3 (.in_1(add8u_2_out_3), .in_2(sl_r_l_1_3_out_3), .out_3(add8u_3_out_3));  // open: out_4, out_5
  SL_R_L_1 sl_r_l_1_4 (.in_1(multiply8x1u_5_out_3), .in_2(1'b0), .out_3(sl_r_l_1_4_out_3));
  ADD8u add8u_4 (.in_1(add8u_3_out_3), .in_2(sl_r_l_1_4_out_3), .out_3(add8u_4_out_3));  // open: out_4, out_5
  SL_R_L_1 sl_r_l_1_5 (.in_1(multiply8x1u_6_out_3), .in_2(1'b0), .out_3(sl_r_l_1_5_out_3));
  ADD8u add8u_5 (.in_1(add8u_4_out_3), .in_2(sl_r_l_1_5_out_3), .out_3(add8u_5_out_3));  // open: out_4, out_5
  SL_R_L_1 sl_r_l_1_6 (.in_1(multiply8x1u_7_out_3), .in_2(1'b0), .out_3(sl_r_l_1_6_out_3));
  ADD8u add8u_6 (.in_1(add8u_5_out_3), .in_2(sl_r_l_1_6_out_3), .out_3(add8u_6_out_3));  // open: out_4, out_5
  SL_R_L_1 sl_r_l_1_7 (.in_1(multiply8x1u_8_out_3), .in_2(1'b0), .out_3(sl_r_l_1_7_out_3));
  ADD8u add8u_7 (.in_1(add8u_6_out_3), .in_2(sl_r_l_1_7_out_3), .out_3(out_3));  // open: out_4, out_5
endmodule

module Multiply8x1u (
  input  in_1,
  input  [7:0] in_2,
  output [7:0] out_3
);

  and and_1 (out_3[0], in_1, in_2[0]);
  and and_2 (out_3[1], in_1, in_2[1]);
  and and_3 (out_3[2], in_1, in_2[2]);
  and and_4 (out_3[3], in_1, in_2[3]);
  and and_5 (out_3[4], in_1, in_2[4]);
  and and_6 (out_3[5], in_1, in_2[5]);
  and and_7 (out_3[6], in_1, in_2[6]);
  and and_8 (out_3[7], in_1, in_2[7]);
endmodule

module Distract8u (
  input  [7:0] in_1,
  input  in_2,
  input  [7:0] in_3,
  output [7:0] out_4
);

  wire and_1_out, not_1_out;
  wire [7:0] additionalcode8_1_out_2, multiplexer_1_out;

  not not_1 (not_1_out, in_3[7]);
  AdditionalCode8 additionalcode8_1 (.in_1(in_3), .out_2(additionalcode8_1_out_2));
  and and_1 (and_1_out, in_2, not_1_out);
  Multiplexer #(.width(8), .enable("false")) multiplexer_1 (
    .in0(in_3), .in1(additionalcode8_1_out_2), .out(multiplexer_1_out), .sel(and_1_out));
  ADD8u add8u_1 (.in_1(in_1), .in_2(multiplexer_1_out), .out_3(out_4));  // open: out_4, out_5
endmodule

module AdditionalCode8 (
  input  [7:0] in_1,
  output [7:0] out_2
);

  wire [7:0] not_1_out;

  assign not_1_out = ~in_1;  // NOT_Gate not_1, 8 bits wide
  ADD8u add8u_1 (.in_1(not_1_out), .in_2(8'h1), .out_3(out_2));  // open: out_4, out_5
endmodule

module MUX8bitx1bit (
  input  [7:0] in_1,
  input  in_2,
  input  [7:0] in_3,
  output [7:0] out_4
);

  wire not_1_out;
  wire [7:0] and_2_out, and_4_out;

  and and_1 (and_2_out[1], in_1[1], not_1_out);
  and and_2 (and_2_out[0], in_1[0], not_1_out);
  not not_1 (not_1_out, in_2);
  and and_3 (and_4_out[1], in_3[1], in_2);
  and and_4 (and_4_out[0], in_3[0], in_2);
  and and_5 (and_2_out[2], in_1[2], not_1_out);
  and and_6 (and_2_out[4], in_1[4], not_1_out);
  and and_7 (and_2_out[3], in_1[3], not_1_out);
  and and_8 (and_4_out[4], in_3[4], in_2);
  and and_9 (and_4_out[3], in_3[3], in_2);
  and and_10 (and_4_out[2], in_3[2], in_2);
  and and_11 (and_2_out[6], in_1[6], not_1_out);
  and and_12 (and_2_out[7], in_1[7], not_1_out);
  and and_13 (and_2_out[5], in_1[5], not_1_out);
  and and_14 (and_4_out[6], in_3[6], in_2);
  and and_15 (and_4_out[5], in_3[5], in_2);
  and and_16 (and_4_out[7], in_3[7], in_2);
  assign out_4 = and_2_out | and_4_out;  // OR_Gate or_1, 8 bits wide
endmodule

module MUX8bitx2bit (
  input  [7:0] in_1,
  input  [7:0] in_2,
  input  [7:0] in_3,
  input  [7:0] in_4,
  input  [1:0] in_5,
  output [7:0] out_6
);

  wire [7:0] mux8bitx1bit_1_out_4, mux8bitx1bit_2_out_4;

  MUX8bitx1bit mux8bitx1bit_1 (.in_1(in_1), .in_3(in_2), .in_2(in_5[0]), .out_4(mux8bitx1bit_1_out_4));
  MUX8bitx1bit mux8bitx1bit_2 (.in_1(in_3), .in_3(in_4), .in_2(in_5[0]), .out_4(mux8bitx1bit_2_out_4));
  MUX8bitx1bit mux8bitx1bit_3 (.in_1(mux8bitx1bit_1_out_4), .in_3(mux8bitx1bit_2_out_4), .in_2(in_5[1]), .out_4(out_6));
endmodule

module DEMUX8bitx1bit (
  input  [7:0] in_1,
  input  in_2,
  output [7:0] out_3,
  output [7:0] out_4
);

  wire not_1_out;

  and and_1 (out_3[0], in_1[0], not_1_out);
  and and_2 (out_3[1], in_1[1], not_1_out);
  not not_1 (not_1_out, in_2);
  and and_3 (out_4[1], in_1[1], in_2);
  and and_4 (out_4[0], in_1[0], in_2);
  and and_5 (out_3[3], in_1[3], not_1_out);
  and and_6 (out_3[2], in_1[2], not_1_out);
  and and_7 (out_4[2], in_1[2], in_2);
  and and_8 (out_4[3], in_1[3], in_2);
  and and_9 (out_3[5], in_1[5], not_1_out);
  and and_10 (out_3[6], in_1[6], not_1_out);
  and and_11 (out_3[4], in_1[4], not_1_out);
  and and_12 (out_4[4], in_1[4], in_2);
  and and_13 (out_4[5], in_1[5], in_2);
  and and_14 (out_4[6], in_1[6], in_2);
  and and_15 (out_3[7], in_1[7], not_1_out);
  and and_16 (out_4[7], in_1[7], in_2);
endmodule

module DEMUX8bitx2bit (
  input  [7:0] in_1,
  input  [1:0] in_2,
  output [7:0] out_3,
  output [7:0] out_4,
  output [7:0] out_5,
  output [7:0] out_6
);

  wire [7:0] demux8bitx1bit_1_out_3, demux8bitx1bit_1_out_4;

  DEMUX8bitx1bit demux8bitx1bit_1 (
    .in_2(in_2[0]), .in_1(in_1), .out_3(demux8bitx1bit_1_out_3), .out_4(demux8bitx1bit_1_out_4));
  DEMUX8bitx1bit demux8bitx1bit_2 (.in_2(in_2[1]), .in_1(demux8bitx1bit_1_out_3), .out_3(out_3), .out_4(out_5));
  DEMUX8bitx1bit demux8bitx1bit_3 (.in_2(in_2[1]), .in_1(demux8bitx1bit_1_out_4), .out_3(out_4), .out_4(out_6));
endmodule

module SL_R_L_1 (
  input  [7:0] in_1,
  input  in_2,
  output [7:0] out_3
);

  wire and_2_out, and_3_out, and_4_out, and_5_out, and_6_out, and_7_out, and_8_out, and_9_out, and_10_out,
       and_11_out, and_13_out, and_14_out, not_1_out;

  not not_1 (not_1_out, in_2);
  and and_1 (out_3[7], not_1_out, in_1[6]);
  and and_2 (and_2_out, in_1[7], in_2);
  and and_3 (and_3_out, in_1[6], in_2);
  and and_4 (and_4_out, not_1_out, in_1[5]);
  or or_1 (out_3[6], and_2_out, and_4_out);
  or or_2 (out_3[5], and_3_out, and_6_out);
  and and_5 (and_5_out, in_1[5], in_2);
  and and_6 (and_6_out, not_1_out, in_1[4]);
  or or_3 (out_3[4], and_5_out, and_7_out);
  and and_7 (and_7_out, not_1_out, in_1[3]);
  and and_8 (and_8_out, in_1[4], in_2);
  or or_4 (out_3[3], and_8_out, and_10_out);
  and and_9 (and_9_out, in_1[3], in_2);
  and and_10 (and_10_out, not_1_out, in_1[2]);
  or or_5 (out_3[2], and_9_out, and_13_out);
  and and_11 (and_11_out, in_1[2], in_2);
  and and_12 (out_3[0], in_1[1], in_2);
  and and_13 (and_13_out, not_1_out, in_1[1]);
  or or_6 (out_3[1], and_11_out, and_14_out);
  and and_14 (and_14_out, not_1_out, in_1[0]);
endmodule

module SC_CL_CR_1 (
  input  [7:0] in_1,
  input  in_2,
  output [7:0] out_3
);

  wire _1, _2, and_2_out, and_3_out, and_4_out, and_5_out, and_6_out, and_7_out, and_8_out, and_9_out,
       and_10_out, and_11_out, and_12_out, and_13_out, and_14_out, and_16_out, not_1_out;

  not not_1 (not_1_out, in_2);
  and and_1 (_1, not_1_out, in_1[7]);
  and and_2 (and_2_out, in_1[7], in_2);
  and and_3 (and_3_out, not_1_out, in_1[6]);
  or or_1 (out_3[7], _2, and_3_out);
  and and_4 (and_4_out, in_1[6], in_2);
  and and_5 (and_5_out, not_1_out, in_1[5]);
  or or_2 (out_3[6], and_2_out, and_5_out);
  or or_3 (out_3[5], and_4_out, and_6_out);
  and and_6 (and_6_out, not_1_out, in_1[4]);
  and and_7 (and_7_out, in_1[5], in_2);
  or or_4 (out_3[4], and_7_out, and_9_out);
  and and_8 (and_8_out, in_1[4], in_2);
  and and_9 (and_9_out, not_1_out, in_1[3]);
  or or_5 (out_3[3], and_8_out, and_10_out);
  and and_10 (and_10_out, not_1_out, in_1[2]);
  and and_11 (and_11_out, in_1[3], in_2);
  or or_6 (out_3[2], and_11_out, and_12_out);
  and and_12 (and_12_out, not_1_out, in_1[1]);
  and and_13 (and_13_out, in_1[2], in_2);
  and and_14 (and_14_out, in_1[1], in_2);
  or or_7 (out_3[1], and_13_out, and_16_out);
  and and_15 (_2, in_1[0], in_2);
  and and_16 (and_16_out, not_1_out, in_1[0]);
  or or_8 (out_3[0], and_14_out, _1);
endmodule

module SA_R_L_1 (
  input  [7:0] in_1,
  input  in_2,
  output [7:0] out_3
);

  wire and_1_out, and_2_out, and_3_out, and_4_out, and_5_out, and_6_out, and_7_out, and_8_out, and_9_out,
       and_10_out, and_11_out, and_12_out, and_14_out, not_1_out;

  not not_1 (not_1_out, in_2);
  and and_1 (and_1_out, not_1_out, in_1[6]);
  and and_2 (and_2_out, in_1[7], in_2);
  or or_1 (out_3[7], and_2_out, and_1_out);
  and and_3 (and_3_out, in_1[6], in_2);
  and and_4 (and_4_out, not_1_out, in_1[5]);
  or or_2 (out_3[6], and_2_out, and_4_out);
  or or_3 (out_3[5], and_3_out, and_5_out);
  and and_5 (and_5_out, not_1_out, in_1[4]);
  and and_6 (and_6_out, in_1[5], in_2);
  or or_4 (out_3[4], and_6_out, and_7_out);
  and and_7 (and_7_out, not_1_out, in_1[3]);
  and and_8 (and_8_out, in_1[4], in_2);
  or or_5 (out_3[3], and_8_out, and_10_out);
  and and_9 (and_9_out, in_1[3], in_2);
  and and_10 (and_10_out, not_1_out, in_1[2]);
  or or_6 (out_3[2], and_9_out, and_11_out);
  and and_11 (and_11_out, not_1_out, in_1[1]);
  and and_12 (and_12_out, in_1[2], in_2);
  and and_13 (out_3[0], in_1[1], in_2);
  or or_7 (out_3[1], and_12_out, and_14_out);
  and and_14 (and_14_out, not_1_out, in_1[0]);
endmodule

module RS_trigger (
  input  in_1,
  input  in_2,
  output out_3,
  output out_4
);

  nor nor_1 (out_3, in_1, out_4);
  nor nor_2 (out_4, in_2, out_3);
endmodule

module D_trigger (
  input  in_1,
  input  in_2,
  output out_3,
  output out_4
);

  wire and_1_out, and_2_out, not_1_out;

  and and_1 (and_1_out, in_1, not_1_out);
  not not_1 (not_1_out, in_2);
  and and_2 (and_2_out, in_1, in_2);
  RS_trigger rs_trigger_1 (.in_1(and_1_out), .in_2(and_2_out), .out_3(out_3), .out_4(out_4));
endmodule

module Flip_Flop (
  input  in_1,
  input  in_2,
  output out_3
);

  wire d_trigger_1_out_3, not_1_out;

  not not_1 (not_1_out, in_1);
  D_trigger d_trigger_1 (.in_2(in_2), .in_1(not_1_out), .out_3(d_trigger_1_out_3));  // open: out_4
  D_trigger d_trigger_2 (.in_2(d_trigger_1_out_3), .in_1(in_1), .out_3(out_3));  // open: out_4
endmodule

module Register (
  input  in_1,
  input  in_2,
  input  [7:0] in_3,
  output [7:0] out_4
);

  wire and_1_out;

  and and_1 (and_1_out, in_1, in_2);
  Flip_Flop ff_1 (.in_2(in_3[0]), .in_1(and_1_out), .out_3(out_4[0]));
  Flip_Flop ff_2 (.in_2(in_3[1]), .in_1(and_1_out), .out_3(out_4[1]));
  Flip_Flop ff_3 (.in_2(in_3[2]), .in_1(and_1_out), .out_3(out_4[2]));
  Flip_Flop ff_4 (.in_2(in_3[3]), .in_1(and_1_out), .out_3(out_4[3]));
  Flip_Flop ff_5 (.in_2(in_3[4]), .in_1(and_1_out), .out_3(out_4[4]));
  Flip_Flop ff_6 (.in_2(in_3[5]), .in_1(and_1_out), .out_3(out_4[5]));
  Flip_Flop ff_7 (.in_2(in_3[6]), .in_1(and_1_out), .out_3(out_4[6]));
  Flip_Flop ff_8 (.in_2(in_3[7]), .in_1(and_1_out), .out_3(out_4[7]));
endmodule

module Counter (
  input  in_1,
  input  [7:0] in_2,
  output [7:0] out_3
);

  wire adder_1_cout, and_1_out, clock_1_out, multiplexer_1_out, not_1_out, not_2_out;
  wire [7:0] adder_1_out, transistor_1_out;

  not not_1 (not_1_out, in_1);
  Transistor #(.width(8)) transistor_1 (.in(adder_1_out), .out(transistor_1_out), .gate(not_1_out));
  Register_part register_1 (.D(transistor_1_out), .Q(out_3), .clk(and_1_out));  // open: en, clr
  and and_1 (and_1_out, clock_1_out, not_2_out);
  Transistor #(.width(8)) transistor_2 (.in(in_2), .out(transistor_1_out), .gate(in_1));
  not not_2 (not_2_out, multiplexer_1_out);
  Clock clock_1 (.out(clock_1_out));
  Multiplexer #(.enable("false")) multiplexer_1 (.in0(in_1), .in1(adder_1_cout), .out(multiplexer_1_out), .sel(in_1));
  Adder adder_1 (.a(8'h1), .b(out_3), .out(adder_1_out), .cout(adder_1_cout));  // open: cin
endmodule

module IsBigger1 (
  input  in_1,
  input  in_2,
  output out_3
);

  wire and_1_out, xor_1_out;

  and and_1 (and_1_out, in_1, 1'b1);
  xor xor_1 (xor_1_out, in_1, in_2);
  and and_2 (out_3, and_1_out, xor_1_out);
endmodule

module Bigger_Equal_Less (
  input  in_1,
  input  in_2,
  output out_3,
  output out_4,
  output out_5
);

  wire xor_1_out;

  xor xor_1 (xor_1_out, in_1, in_2);
  and and_1 (out_3, in_1, xor_1_out);
  not not_1 (out_4, xor_1_out);
  and and_2 (out_5, xor_1_out, in_2);
endmodule

module Comp8u (
  input  [7:0] in_1,
  input  [7:0] in_2,
  input  in_3,
  output A____B,
  output A___B,
  output A____B_2,
  output A___B_2,
  output A___B_3,
  output A____B_3
);

  wire and_1_out, and_2_out, and_3_out, and_4_out, and_5_out, and_6_out, and_7_out,
       bigger_equal_less_1_out_3, bigger_equal_less_1_out_4, bigger_equal_less_1_out_5,
       bigger_equal_less_2_out_3, bigger_equal_less_2_out_4, bigger_equal_less_2_out_5,
       bigger_equal_less_3_out_3, bigger_equal_less_3_out_4, bigger_equal_less_3_out_5,
       bigger_equal_less_4_out_3, bigger_equal_less_4_out_4, bigger_equal_less_4_out_5,
       bigger_equal_less_5_out_3, bigger_equal_less_5_out_4, bigger_equal_less_5_out_5,
       bigger_equal_less_6_out_3, bigger_equal_less_6_out_4, bigger_equal_less_6_out_5,
       bigger_equal_less_7_out_3, bigger_equal_less_7_out_4, bigger_equal_less_7_out_5,
       bigger_equal_less_8_out_3, bigger_equal_less_8_out_4, bigger_equal_less_8_out_5, changesign_1_out_4,
       changesign_1_out_5, not_1_out, not_2_out, not_3_out, not_4_out, not_5_out, not_6_out, not_7_out,
       not_8_out, not_9_out, not_12_out;

  ChangeSign changesign_1 (
    .in_3(in_3), .in_1(in_2[7]), .in_2(in_1[7]), .out_4(changesign_1_out_4), .out_5(changesign_1_out_5));
  not not_1 (not_1_out, bigger_equal_less_2_out_5);
  Bigger_Equal_Less bigger_equal_less_1 (
    .in_1(in_1[6]), .in_2(in_2[6]), .out_3(bigger_equal_less_1_out_3), .out_4(bigger_equal_less_1_out_4),
    .out_5(bigger_equal_less_1_out_5));
  Bigger_Equal_Less bigger_equal_less_2 (
    .in_1(changesign_1_out_5), .in_2(changesign_1_out_4), .out_3(bigger_equal_less_2_out_3),
    .out_4(bigger_equal_less_2_out_4), .out_5(bigger_equal_less_2_out_5));
  not not_2 (not_2_out, bigger_equal_less_1_out_5);
  and and_1 (and_1_out, not_1_out, bigger_equal_less_1_out_3);
  Bigger_Equal_Less bigger_equal_less_3 (
    .in_1(in_1[5]), .in_2(in_2[5]), .out_3(bigger_equal_less_3_out_3), .out_4(bigger_equal_less_3_out_4),
    .out_5(bigger_equal_less_3_out_5));
  not not_3 (not_3_out, bigger_equal_less_3_out_5);
  and and_2 (and_2_out, not_1_out, not_2_out, bigger_equal_less_3_out_3);
  Bigger_Equal_Less bigger_equal_less_4 (
    .in_1(in_1[4]), .in_2(in_2[4]), .out_3(bigger_equal_less_4_out_3), .out_4(bigger_equal_less_4_out_4),
    .out_5(bigger_equal_less_4_out_5));
  not not_4 (not_4_out, bigger_equal_less_4_out_5);
  and and_3 (and_3_out, not_1_out, not_2_out, not_3_out, bigger_equal_less_4_out_3);
  Bigger_Equal_Less bigger_equal_less_5 (
    .in_1(in_1[3]), .in_2(in_2[3]), .out_3(bigger_equal_less_5_out_3), .out_4(bigger_equal_less_5_out_4),
    .out_5(bigger_equal_less_5_out_5));
  not not_5 (not_5_out, bigger_equal_less_5_out_5);
  and and_4 (and_4_out, not_1_out, not_2_out, not_3_out, not_4_out, bigger_equal_less_5_out_3);
  Bigger_Equal_Less bigger_equal_less_6 (
    .in_1(in_1[2]), .in_2(in_2[2]), .out_3(bigger_equal_less_6_out_3), .out_4(bigger_equal_less_6_out_4),
    .out_5(bigger_equal_less_6_out_5));
  not not_6 (not_6_out, bigger_equal_less_6_out_5);
  and and_5 (and_5_out, not_1_out, not_2_out, not_3_out, not_4_out, not_5_out, bigger_equal_less_6_out_3);
  Bigger_Equal_Less bigger_equal_less_7 (
    .in_1(in_1[1]), .in_2(in_2[1]), .out_3(bigger_equal_less_7_out_3), .out_4(bigger_equal_less_7_out_4),
    .out_5(bigger_equal_less_7_out_5));
  not not_7 (not_7_out, bigger_equal_less_7_out_5);
  and and_6 (and_6_out, not_1_out, not_2_out, not_3_out, not_4_out, not_5_out, not_6_out, bigger_equal_less_7_out_3);
  Bigger_Equal_Less bigger_equal_less_8 (
    .in_1(in_1[0]), .in_2(in_2[0]), .out_3(bigger_equal_less_8_out_3), .out_4(bigger_equal_less_8_out_4),
    .out_5(bigger_equal_less_8_out_5));
  not not_8 (not_8_out, bigger_equal_less_8_out_5);
  and and_7 (and_7_out, not_1_out, not_2_out, not_3_out, not_4_out, not_5_out, not_6_out, not_7_out, not_8_out, bigger_equal_less_8_out_3);
  or or_1 (A___B_3, bigger_equal_less_2_out_3, and_1_out, and_2_out, and_3_out, and_4_out, and_5_out, and_6_out, and_7_out);
  not not_9 (not_9_out, A___B_3);
  not not_10 (A____B_3, A___B_3);
  not not_11 (A____B, A___B);
  and and_8 (A___B, bigger_equal_less_8_out_4, bigger_equal_less_7_out_4, bigger_equal_less_6_out_4, bigger_equal_less_5_out_4, bigger_equal_less_4_out_4, bigger_equal_less_3_out_4, bigger_equal_less_1_out_4, bigger_equal_less_2_out_4);
  or or_2 (A____B_2, A___B, A___B_3);
  not not_12 (not_12_out, A___B);
  and and_9 (A___B_2, not_9_out, not_12_out);
endmodule

module ChangeSign (
  input  in_1,
  input  in_2,
  input  in_3,
  output out_4,
  output out_5
);

  wire and_1_out, xor_1_out;

  xor xor_1 (xor_1_out, in_1, in_2);
  and and_1 (and_1_out, in_3, xor_1_out);
  ADD1 add1_1 (.in_1(1'b0), .\х1 (in_1), .\х2 (and_1_out), .\Значащий (out_4));  // open: Смещение
  ADD1 add1_2 (.in_1(1'b0), .\х1 (in_2), .\х2 (and_1_out), .\Значащий (out_5));  // open: Смещение
endmodule

module Multiply8x8s (
  input  [7:0] in_1,
  input  [7:0] in_2,
  output [7:0] out_3
);

  wire \s_add_1_младший ;
  wire [7:0] forwardcode8_1_out_2, forwardcode8_2_out_2, forwardcode8_3_out_2, multiplexer_1_out,
       multiplexer_2_out, multiply8x8u_1_out_3;

  ForwardCode8 forwardcode8_1 (.in_1(in_1), .out_2(forwardcode8_1_out_2));
  ForwardCode8 forwardcode8_2 (.in_1(in_2), .out_2(forwardcode8_2_out_2));
  Multiplexer #(.width(8), .enable("false")) multiplexer_1 (
    .in0(in_1), .in1(forwardcode8_1_out_2), .out(multiplexer_1_out), .sel(in_1[7]));
  Multiplexer #(.width(8), .enable("false")) multiplexer_2 (
    .in0(in_2), .in1(forwardcode8_2_out_2), .out(multiplexer_2_out), .sel(in_2[7]));
  Multiply8x8u multiply8x8u_1 (.in_1(multiplexer_1_out), .in_2(multiplexer_2_out), .out_3(multiply8x8u_1_out_3));
  S_ADD s_add_1 (.\х1 (in_1[7]), .\х2 (in_2[7]), .\Младший (\s_add_1_младший ));  // open: Смещение
  Multiplexer #(.width(8), .enable("false")) multiplexer_3 (
    .in0(multiply8x8u_1_out_3), .in1(forwardcode8_3_out_2), .out(out_3), .sel(\s_add_1_младший ));
  ForwardCode8 forwardcode8_3 (.in_1(multiply8x8u_1_out_3), .out_2(forwardcode8_3_out_2));
endmodule

module ForwardCode8 (
  input  [7:0] in_1,
  output [7:0] out_2
);

  wire [7:0] subtractor_1_out;

  Subtractor subtractor_1 (.a(in_1), .b(8'h1), .out(subtractor_1_out));  // open: bin, bout
  assign out_2 = ~subtractor_1_out;  // NOT_Gate not_1, 8 bits wide
endmodule

module bin_op (
  input  [7:0] in_1,
  input  [7:0] in_2,
  input  [7:0] in_3,
  input  [7:0] in_4,
  input  [7:0] in_5,
  input  [7:0] in_6,
  input  [7:0] in_7,
  output [7:0] out_8,
  output [7:0] out_9,
  output [7:0] out_10,
  output [7:0] out_11
);

  wire [7:0] and_2_out, and_3_out, and_4_out, and_5_out, and_6_out, not_1_out, not_3_out, not_4_out;

  assign out_8 = in_1 & in_3;  // AND_Gate and_1, 8 bits wide
  assign and_2_out = in_5 & in_6;  // AND_Gate and_2, 8 bits wide
  assign not_1_out = ~and_2_out;  // NOT_Gate not_1, 8 bits wide
  assign and_3_out = in_7 & in_7;  // AND_Gate and_3, 8 bits wide
  assign out_11 = ~and_3_out;  // NOT_Gate not_2, 8 bits wide
  assign not_3_out = ~and_4_out;  // NOT_Gate not_3, 8 bits wide
  assign and_4_out = in_5 & not_1_out;  // AND_Gate and_4, 8 bits wide
  assign not_4_out = ~and_5_out;  // NOT_Gate not_4, 8 bits wide
  assign and_5_out = not_1_out & in_6;  // AND_Gate and_5, 8 bits wide
  assign out_10 = ~and_6_out;  // NOT_Gate not_5, 8 bits wide
  assign and_6_out = not_3_out & not_4_out;  // AND_Gate and_6, 8 bits wide
  assign out_9 = in_2 | in_4;  // OR_Gate or_1, 8 bits wide

  // Notes on the sheet:
  //   ~
  //   ^
endmodule

module logic_op (
  input  [7:0] in_1,
  input  [7:0] in_2,
  input  [7:0] in_3,
  input  [7:0] in_4,
  input  [7:0] in_5,
  input  [7:0] in_6,
  input  [7:0] in_7,
  output out_8,
  output out_9,
  output out_10,
  output out_11
);

  wire [7:0] and_1_out, and_2_out, and_3_out, and_4_out, and_5_out, and_6_out, not_1_out, not_2_out,
       not_3_out, not_4_out, not_5_out, or_4_out;

  assign and_1_out = in_2 & in_4;  // AND_Gate and_1, 8 bits wide
  assign and_2_out = in_5 & in_6;  // AND_Gate and_2, 8 bits wide
  assign not_1_out = ~and_2_out;  // NOT_Gate not_1, 8 bits wide
  assign and_3_out = in_7 & in_7;  // AND_Gate and_3, 8 bits wide
  assign not_2_out = ~and_3_out;  // NOT_Gate not_2, 8 bits wide
  or or_1 (out_9, and_1_out[0], and_1_out[1], and_1_out[2], and_1_out[3], and_1_out[4], and_1_out[5], and_1_out[6], and_1_out[7]);
  assign not_3_out = ~and_4_out;  // NOT_Gate not_3, 8 bits wide
  assign and_4_out = in_5 & not_1_out;  // AND_Gate and_4, 8 bits wide
  assign and_5_out = not_1_out & in_6;  // AND_Gate and_5, 8 bits wide
  assign not_4_out = ~and_5_out;  // NOT_Gate not_4, 8 bits wide
  assign and_6_out = not_3_out & not_4_out;  // AND_Gate and_6, 8 bits wide
  assign not_5_out = ~and_6_out;  // NOT_Gate not_5, 8 bits wide
  or or_2 (out_11, not_2_out[0], not_2_out[1], not_2_out[2], not_2_out[3], not_2_out[4], not_2_out[5], not_2_out[6], not_2_out[7]);
  or or_3 (out_10, not_5_out[0], not_5_out[1], not_5_out[2], not_5_out[3], not_5_out[4], not_5_out[5], not_5_out[6], not_5_out[7]);
  assign or_4_out = in_1 | in_3;  // OR_Gate or_4, 8 bits wide
  or or_5 (out_8, or_4_out[0], or_4_out[1], or_4_out[2], or_4_out[3], or_4_out[4], or_4_out[5], or_4_out[6], or_4_out[7]);

  // Notes on the sheet:
  //   ~
  //   ^
endmodule

module SLx8 (
  input  [2:0] in_1,
  input  in_2,
  input  [7:0] in_3,
  output [7:0] out_4
);

  wire [7:0] demultiplexer_1_out0, demultiplexer_1_out1, demultiplexer_2_out0, demultiplexer_2_out1,
       demultiplexer_3_out0, demultiplexer_3_out1, multiplexer_1_out, multiplexer_2_out, sl_r_l_1_1_out_3,
       sl_r_l_1_2_out_3, sl_r_l_1_3_out_3, sl_r_l_1_4_out_3, sl_r_l_1_5_out_3, sl_r_l_1_6_out_3,
       sl_r_l_1_7_out_3;

  Demultiplexer #(.width(8), .enable("false")) demultiplexer_1 (
    .out0(demultiplexer_1_out0), .out1(demultiplexer_1_out1), .in(in_3), .sel(in_1[0]));
  SL_R_L_1 sl_r_l_1_1 (.in_1(demultiplexer_1_out1), .in_2(in_2), .out_3(sl_r_l_1_1_out_3));
  Multiplexer #(.width(8), .enable("false")) multiplexer_1 (
    .in0(demultiplexer_1_out0), .in1(sl_r_l_1_1_out_3), .out(multiplexer_1_out), .sel(in_1[0]));
  Demultiplexer #(.width(8), .enable("false")) demultiplexer_2 (
    .out0(demultiplexer_2_out0), .out1(demultiplexer_2_out1), .in(multiplexer_1_out), .sel(in_1[1]));
  SL_R_L_1 sl_r_l_1_2 (.in_1(demultiplexer_2_out1), .in_2(in_2), .out_3(sl_r_l_1_2_out_3));
  SL_R_L_1 sl_r_l_1_3 (.in_1(sl_r_l_1_2_out_3), .in_2(in_2), .out_3(sl_r_l_1_3_out_3));
  Multiplexer #(.width(8), .enable("false")) multiplexer_2 (
    .in0(demultiplexer_2_out0), .in1(sl_r_l_1_3_out_3), .out(multiplexer_2_out), .sel(in_1[1]));
  Demultiplexer #(.width(8), .enable("false")) demultiplexer_3 (
    .out0(demultiplexer_3_out0), .out1(demultiplexer_3_out1), .in(multiplexer_2_out), .sel(in_1[2]));
  SL_R_L_1 sl_r_l_1_4 (.in_1(demultiplexer_3_out1), .in_2(in_2), .out_3(sl_r_l_1_4_out_3));
  SL_R_L_1 sl_r_l_1_5 (.in_1(sl_r_l_1_4_out_3), .in_2(in_2), .out_3(sl_r_l_1_5_out_3));
  SL_R_L_1 sl_r_l_1_6 (.in_1(sl_r_l_1_7_out_3), .in_2(in_2), .out_3(sl_r_l_1_6_out_3));
  SL_R_L_1 sl_r_l_1_7 (.in_1(sl_r_l_1_5_out_3), .in_2(in_2), .out_3(sl_r_l_1_7_out_3));
  Multiplexer #(.width(8), .enable("false")) multiplexer_3 (
    .in0(demultiplexer_3_out0), .in1(sl_r_l_1_6_out_3), .out(out_4), .sel(in_1[2]));
endmodule

module SAx8 (
  input  [2:0] in_1,
  input  in_2,
  input  [7:0] in_3,
  output [7:0] out_4
);

  wire [7:0] demultiplexer_1_out0, demultiplexer_1_out1, demultiplexer_2_out0, demultiplexer_2_out1,
       demultiplexer_3_out0, demultiplexer_3_out1, multiplexer_1_out, multiplexer_2_out, sa_r_l_1_1_out_3,
       sa_r_l_1_2_out_3, sa_r_l_1_3_out_3, sa_r_l_1_4_out_3, sa_r_l_1_5_out_3, sa_r_l_1_6_out_3,
       sa_r_l_1_7_out_3;

  Demultiplexer #(.width(8), .enable("false")) demultiplexer_1 (
    .out0(demultiplexer_1_out0), .out1(demultiplexer_1_out1), .in(in_3), .sel(in_1[0]));
  SA_R_L_1 sa_r_l_1_1 (.in_1(demultiplexer_1_out1), .in_2(in_2), .out_3(sa_r_l_1_1_out_3));
  Multiplexer #(.width(8), .enable("false")) multiplexer_1 (
    .in0(demultiplexer_1_out0), .in1(sa_r_l_1_1_out_3), .out(multiplexer_1_out), .sel(in_1[0]));
  Demultiplexer #(.width(8), .enable("false")) demultiplexer_2 (
    .out0(demultiplexer_2_out0), .out1(demultiplexer_2_out1), .in(multiplexer_1_out), .sel(in_1[1]));
  SA_R_L_1 sa_r_l_1_2 (.in_1(demultiplexer_2_out1), .in_2(in_2), .out_3(sa_r_l_1_2_out_3));
  SA_R_L_1 sa_r_l_1_3 (.in_1(sa_r_l_1_2_out_3), .in_2(in_2), .out_3(sa_r_l_1_3_out_3));
  Multiplexer #(.width(8), .enable("false")) multiplexer_2 (
    .in0(demultiplexer_2_out0), .in1(sa_r_l_1_3_out_3), .out(multiplexer_2_out), .sel(in_1[1]));
  Demultiplexer #(.width(8), .enable("false")) demultiplexer_3 (
    .out0(demultiplexer_3_out0), .out1(demultiplexer_3_out1), .in(multiplexer_2_out), .sel(in_1[2]));
  SA_R_L_1 sa_r_l_1_4 (.in_1(demultiplexer_3_out1), .in_2(in_2), .out_3(sa_r_l_1_4_out_3));
  SA_R_L_1 sa_r_l_1_5 (.in_1(sa_r_l_1_4_out_3), .in_2(in_2), .out_3(sa_r_l_1_5_out_3));
  SA_R_L_1 sa_r_l_1_6 (.in_1(sa_r_l_1_5_out_3), .in_2(in_2), .out_3(sa_r_l_1_6_out_3));
  SA_R_L_1 sa_r_l_1_7 (.in_1(sa_r_l_1_6_out_3), .in_2(in_2), .out_3(sa_r_l_1_7_out_3));
  Multiplexer #(.width(8), .enable("false")) multiplexer_3 (
    .in0(demultiplexer_3_out0), .in1(sa_r_l_1_7_out_3), .out(out_4), .sel(in_1[2]));
endmodule

module SCx8 (
  input  [2:0] in_1,
  input  in_2,
  input  [7:0] in_3,
  output [7:0] out_4
);

  wire [7:0] demultiplexer_1_out0, demultiplexer_1_out1, demultiplexer_2_out0, demultiplexer_2_out1,
       demultiplexer_3_out0, demultiplexer_3_out1, multiplexer_1_out, multiplexer_2_out, sc_cl_cr_1_1_out_3,
       sc_cl_cr_1_2_out_3, sc_cl_cr_1_3_out_3, sc_cl_cr_1_4_out_3, sc_cl_cr_1_5_out_3, sc_cl_cr_1_6_out_3,
       sc_cl_cr_1_7_out_3;

  Demultiplexer #(.width(8), .enable("false")) demultiplexer_1 (
    .out0(demultiplexer_1_out0), .out1(demultiplexer_1_out1), .in(in_3), .sel(in_1[0]));
  SC_CL_CR_1 sc_cl_cr_1_1 (.in_1(demultiplexer_1_out1), .in_2(in_2), .out_3(sc_cl_cr_1_1_out_3));
  Multiplexer #(.width(8), .enable("false")) multiplexer_1 (
    .in0(demultiplexer_1_out0), .in1(sc_cl_cr_1_1_out_3), .out(multiplexer_1_out), .sel(in_1[0]));
  Demultiplexer #(.width(8), .enable("false")) demultiplexer_2 (
    .out0(demultiplexer_2_out0), .out1(demultiplexer_2_out1), .in(multiplexer_1_out), .sel(in_1[1]));
  SC_CL_CR_1 sc_cl_cr_1_2 (.in_1(demultiplexer_2_out1), .in_2(in_2), .out_3(sc_cl_cr_1_2_out_3));
  SC_CL_CR_1 sc_cl_cr_1_3 (.in_1(sc_cl_cr_1_2_out_3), .in_2(in_2), .out_3(sc_cl_cr_1_3_out_3));
  Multiplexer #(.width(8), .enable("false")) multiplexer_2 (
    .in0(demultiplexer_2_out0), .in1(sc_cl_cr_1_3_out_3), .out(multiplexer_2_out), .sel(in_1[1]));
  Demultiplexer #(.width(8), .enable("false")) demultiplexer_3 (
    .out0(demultiplexer_3_out0), .out1(demultiplexer_3_out1), .in(multiplexer_2_out), .sel(in_1[2]));
  SC_CL_CR_1 sc_cl_cr_1_4 (.in_1(demultiplexer_3_out1), .in_2(in_2), .out_3(sc_cl_cr_1_4_out_3));
  SC_CL_CR_1 sc_cl_cr_1_5 (.in_1(sc_cl_cr_1_4_out_3), .in_2(in_2), .out_3(sc_cl_cr_1_5_out_3));
  SC_CL_CR_1 sc_cl_cr_1_6 (.in_1(sc_cl_cr_1_5_out_3), .in_2(in_2), .out_3(sc_cl_cr_1_6_out_3));
  SC_CL_CR_1 sc_cl_cr_1_7 (.in_1(sc_cl_cr_1_6_out_3), .in_2(in_2), .out_3(sc_cl_cr_1_7_out_3));
  Multiplexer #(.width(8), .enable("false")) multiplexer_3 (
    .in0(demultiplexer_3_out0), .in1(sc_cl_cr_1_7_out_3), .out(out_4), .sel(in_1[2]));
endmodule

module division (
  input  [7:0] in_1,
  input  [7:0] in_2,
  output [7:0] out_3,
  output out_4
);

  wire comparator_1_eq, comparator_1_lt, comparator_2_eq, comparator_2_lt, comparator_3_eq, comparator_3_lt,
       comparator_4_eq, comparator_4_lt, comparator_5_eq, comparator_5_lt, comparator_6_eq, comparator_6_lt,
       comparator_7_eq, comparator_7_lt, comparator_8_eq, comparator_8_lt, or_2_out, or_3_out, or_4_out,
       or_5_out, or_6_out, or_7_out, or_8_out, or_9_out;
  wire [7:0] multiplier_1_cout, multiplier_1_out, multiplier_2_cout, multiplier_2_out, multiplier_3_cout,
       multiplier_3_out, multiplier_4_cout, multiplier_4_out, multiplier_5_cout, multiplier_5_out,
       multiplier_6_cout, multiplier_6_out, multiplier_7_cout, multiplier_7_out, multiplier_8_out, or_1_out;

  Multiplier multiplier_1 (.a(in_2), .b(8'h80), .out(multiplier_1_out), .cout(multiplier_1_cout));  // open: cin
  assign or_1_out = in_2 | {8{1'b0}};  // OR_Gate or_1, 8 bits wide
  Comparator #(.mode("unsigned")) comparator_1 (
    .a(multiplier_1_out), .b(in_1), .eq(comparator_1_eq), .lt(comparator_1_lt));  // open: gt
  or or_2 (or_2_out, or_1_out[0], or_1_out[1], or_1_out[2], or_1_out[3], or_1_out[4], or_1_out[5], or_1_out[6], or_1_out[7]);
  or or_3 (or_3_out, comparator_1_eq, comparator_1_lt);
  not not_1 (out_4, or_2_out);
  overflow overflow_1 (.in_1(multiplier_1_cout), .in_2(or_3_out), .out_3(out_3[7]));
  Multiplier multiplier_2 (
    .a({out_3[7], 7'b1000000}), .b(in_2), .out(multiplier_2_out), .cout(multiplier_2_cout));  // open: cin
  Comparator #(.mode("unsigned")) comparator_2 (
    .a(multiplier_2_out), .b(in_1), .eq(comparator_2_eq), .lt(comparator_2_lt));  // open: gt
  overflow overflow_2 (.in_1(multiplier_2_cout), .in_2(or_4_out), .out_3(out_3[6]));
  or or_4 (or_4_out, comparator_2_eq, comparator_2_lt);
  Multiplier multiplier_3 (
    .a({out_3[7:6], 6'b100000}), .b(in_2), .out(multiplier_3_out), .cout(multiplier_3_cout));  // open: cin
  Comparator #(.mode("unsigned")) comparator_3 (
    .a(multiplier_3_out), .b(in_1), .eq(comparator_3_eq), .lt(comparator_3_lt));  // open: gt
  or or_5 (or_5_out, comparator_3_eq, comparator_3_lt);
  overflow overflow_3 (.in_1(multiplier_3_cout), .in_2(or_5_out), .out_3(out_3[5]));
  Multiplier multiplier_4 (
    .a({out_3[7:5], 5'b10000}), .b(in_2), .out(multiplier_4_out), .cout(multiplier_4_cout));  // open: cin
  Comparator #(.mode("unsigned")) comparator_4 (
    .a(multiplier_4_out), .b(in_1), .eq(comparator_4_eq), .lt(comparator_4_lt));  // open: gt
  overflow overflow_4 (.in_1(multiplier_4_cout), .in_2(or_6_out), .out_3(out_3[4]));
  or or_6 (or_6_out, comparator_4_eq, comparator_4_lt);
  Multiplier multiplier_5 (
    .a({out_3[7:4], 4'b1000}), .b(in_2), .out(multiplier_5_out), .cout(multiplier_5_cout));  // open: cin
  Comparator #(.mode("unsigned")) comparator_5 (
    .a(multiplier_5_out), .b(in_1), .eq(comparator_5_eq), .lt(comparator_5_lt));  // open: gt
  overflow overflow_5 (.in_1(multiplier_5_cout), .in_2(or_7_out), .out_3(out_3[3]));
  or or_7 (or_7_out, comparator_5_eq, comparator_5_lt);
  Multiplier multiplier_6 (
    .a({out_3[7:3], 3'b100}), .b(in_2), .out(multiplier_6_out), .cout(multiplier_6_cout));  // open: cin
  overflow overflow_6 (.in_1(multiplier_6_cout), .in_2(or_8_out), .out_3(out_3[2]));
  or or_8 (or_8_out, comparator_6_eq, comparator_6_lt);
  Comparator #(.mode("unsigned")) comparator_6 (
    .a(multiplier_6_out), .b(in_1), .eq(comparator_6_eq), .lt(comparator_6_lt));  // open: gt
  Multiplier multiplier_7 (
    .a({out_3[7:2], 2'b10}), .b(in_2), .out(multiplier_7_out), .cout(multiplier_7_cout));  // open: cin
  Comparator #(.mode("unsigned")) comparator_7 (
    .a(multiplier_7_out), .b(in_1), .eq(comparator_7_eq), .lt(comparator_7_lt));  // open: gt
  or or_9 (or_9_out, comparator_7_eq, comparator_7_lt);
  overflow overflow_7 (.in_1(multiplier_7_cout), .in_2(or_9_out), .out_3(out_3[1]));
  Multiplier multiplier_8 (.a({out_3[7:1], 1'b1}), .b(in_2), .out(multiplier_8_out));  // open: cin, cout
  Comparator #(.mode("unsigned")) comparator_8 (
    .a(multiplier_8_out), .b(in_1), .eq(comparator_8_eq), .lt(comparator_8_lt));  // open: gt
  or or_10 (out_3[0], comparator_8_eq, comparator_8_lt);
endmodule

module logic_or (
  input  [7:0] in_1,
  output out_2
);

  or or_1 (out_2, in_1[0], in_1[1], in_1[2], in_1[3], in_1[4], in_1[5], in_1[6], in_1[7]);
endmodule

module overflow (
  input  [7:0] in_1,
  input  in_2,
  output out_3
);

  wire or_1_out;

  or or_1 (or_1_out, in_1[0], in_1[1], in_1[2], in_1[3], in_1[4], in_1[5], in_1[6], in_1[7]);
  Transistor transistor_1 (.in(in_2), .out(out_3), .gate(or_1_out));
  Pull_Resistor pull_resistor_1 (.node(out_3));
endmodule

module mod (
  input  [7:0] in_1,
  input  [7:0] in_2,
  output [7:0] del,
  output out_4,
  output [7:0] mod
);

  wire [7:0] multiplier_1_out;

  division division_1 (.in_1(in_1), .in_2(in_2), .out_3(del), .out_4(out_4));
  Multiplier multiplier_1 (.a(del), .b(in_2), .out(multiplier_1_out));  // open: cin, cout
  Subtractor subtractor_1 (.a(in_1), .b(multiplier_1_out), .out(mod));  // open: bin, bout
endmodule

module compare_float (
  input  [16:0] in_1,
  input  [16:0] in_2,
  output A____B,
  output A___B,
  output A____B_2,
  output A___B_2,
  output A___B_3,
  output A____B_3
);

  wire and_1_out, and_2_out, bigger_equal_less_1_out_3, bigger_equal_less_1_out_4, bigger_equal_less_1_out_5,
       changesign_1_out_4, changesign_1_out_5, comp_unsigned_1_a___b, comp_unsigned_1_a___b_3,
       comp_unsigned_2_a____b_2, comp_unsigned_2_a___b, comp_unsigned_2_a___b_3, not_1_out, not_2_out,
       not_3_out;

  ChangeSign changesign_1 (
    .in_3(1'b1), .in_1(in_2[0]), .in_2(in_1[0]), .out_4(changesign_1_out_4), .out_5(changesign_1_out_5));
  Bigger_Equal_Less bigger_equal_less_1 (
    .in_1(changesign_1_out_5), .in_2(changesign_1_out_4), .out_3(bigger_equal_less_1_out_3),
    .out_4(bigger_equal_less_1_out_4), .out_5(bigger_equal_less_1_out_5));
  not not_1 (not_1_out, bigger_equal_less_1_out_5);
  comp_unsigned comp_unsigned_1 (
    .in_1(in_1[16:9]), .in_2(in_2[16:9]), .A___B(comp_unsigned_1_a___b), .A___B_3(comp_unsigned_1_a___b_3));  // open: A____B, A____B_2, A___B_2, A____B_3
  comp_unsigned comp_unsigned_2 (
    .in_1(in_1[8:1]), .in_2(in_2[8:1]), .A___B(comp_unsigned_2_a___b), .A____B_2(comp_unsigned_2_a____b_2),
    .A___B_3(comp_unsigned_2_a___b_3));  // open: A____B, A___B_2, A____B_3
  and and_1 (and_1_out, not_1_out, comp_unsigned_2_a____b_2, comp_unsigned_1_a___b_3);
  and and_2 (and_2_out, not_1_out, comp_unsigned_2_a___b_3);
  or or_1 (A___B_3, and_1_out, and_2_out, bigger_equal_less_1_out_3);
  and and_3 (A___B, comp_unsigned_1_a___b, comp_unsigned_2_a___b, bigger_equal_less_1_out_4);
  not not_2 (not_2_out, A___B_3);
  not not_3 (not_3_out, A___B);
  and and_4 (A___B_2, not_2_out, not_3_out);
  not not_4 (A____B_3, A___B_3);
  not not_5 (A____B, A___B);
  or or_2 (A____B_2, A___B, A___B_3);
endmodule

module comp_unsigned (
  input  [7:0] in_1,
  input  [7:0] in_2,
  output A____B,
  output A___B,
  output A____B_2,
  output A___B_2,
  output A___B_3,
  output A____B_3
);

  wire and_1_out, and_2_out, and_3_out, and_4_out, and_5_out, and_6_out, and_7_out,
       bigger_equal_less_1_out_3, bigger_equal_less_1_out_4, bigger_equal_less_1_out_5,
       bigger_equal_less_2_out_3, bigger_equal_less_2_out_4, bigger_equal_less_2_out_5,
       bigger_equal_less_3_out_3, bigger_equal_less_3_out_4, bigger_equal_less_3_out_5,
       bigger_equal_less_4_out_3, bigger_equal_less_4_out_4, bigger_equal_less_4_out_5,
       bigger_equal_less_5_out_3, bigger_equal_less_5_out_4, bigger_equal_less_5_out_5,
       bigger_equal_less_6_out_3, bigger_equal_less_6_out_4, bigger_equal_less_6_out_5,
       bigger_equal_less_7_out_3, bigger_equal_less_7_out_4, bigger_equal_less_7_out_5,
       bigger_equal_less_8_out_3, bigger_equal_less_8_out_4, bigger_equal_less_8_out_5, not_1_out, not_2_out,
       not_3_out, not_4_out, not_5_out, not_6_out, not_7_out, not_8_out, not_9_out, not_12_out;

  not not_1 (not_1_out, bigger_equal_less_1_out_5);
  Bigger_Equal_Less bigger_equal_less_1 (
    .in_1(in_1[7]), .in_2(in_2[7]), .out_3(bigger_equal_less_1_out_3), .out_4(bigger_equal_less_1_out_4),
    .out_5(bigger_equal_less_1_out_5));
  Bigger_Equal_Less bigger_equal_less_2 (
    .in_1(in_1[6]), .in_2(in_2[6]), .out_3(bigger_equal_less_2_out_3), .out_4(bigger_equal_less_2_out_4),
    .out_5(bigger_equal_less_2_out_5));
  not not_2 (not_2_out, bigger_equal_less_2_out_5);
  and and_1 (and_1_out, not_1_out, bigger_equal_less_2_out_3);
  Bigger_Equal_Less bigger_equal_less_3 (
    .in_1(in_1[5]), .in_2(in_2[5]), .out_3(bigger_equal_less_3_out_3), .out_4(bigger_equal_less_3_out_4),
    .out_5(bigger_equal_less_3_out_5));
  not not_3 (not_3_out, bigger_equal_less_3_out_5);
  and and_2 (and_2_out, not_1_out, not_2_out, bigger_equal_less_3_out_3);
  Bigger_Equal_Less bigger_equal_less_4 (
    .in_1(in_1[4]), .in_2(in_2[4]), .out_3(bigger_equal_less_4_out_3), .out_4(bigger_equal_less_4_out_4),
    .out_5(bigger_equal_less_4_out_5));
  not not_4 (not_4_out, bigger_equal_less_4_out_5);
  and and_3 (and_3_out, not_1_out, not_2_out, not_3_out, bigger_equal_less_4_out_3);
  Bigger_Equal_Less bigger_equal_less_5 (
    .in_1(in_1[3]), .in_2(in_2[3]), .out_3(bigger_equal_less_5_out_3), .out_4(bigger_equal_less_5_out_4),
    .out_5(bigger_equal_less_5_out_5));
  not not_5 (not_5_out, bigger_equal_less_5_out_5);
  and and_4 (and_4_out, not_1_out, not_2_out, not_3_out, not_4_out, bigger_equal_less_5_out_3);
  Bigger_Equal_Less bigger_equal_less_6 (
    .in_1(in_1[2]), .in_2(in_2[2]), .out_3(bigger_equal_less_6_out_3), .out_4(bigger_equal_less_6_out_4),
    .out_5(bigger_equal_less_6_out_5));
  not not_6 (not_6_out, bigger_equal_less_6_out_5);
  and and_5 (and_5_out, not_1_out, not_2_out, not_3_out, not_4_out, not_5_out, bigger_equal_less_6_out_3);
  Bigger_Equal_Less bigger_equal_less_7 (
    .in_1(in_1[1]), .in_2(in_2[1]), .out_3(bigger_equal_less_7_out_3), .out_4(bigger_equal_less_7_out_4),
    .out_5(bigger_equal_less_7_out_5));
  not not_7 (not_7_out, bigger_equal_less_7_out_5);
  and and_6 (and_6_out, not_1_out, not_2_out, not_3_out, not_4_out, not_5_out, not_6_out, bigger_equal_less_7_out_3);
  Bigger_Equal_Less bigger_equal_less_8 (
    .in_1(in_1[0]), .in_2(in_2[0]), .out_3(bigger_equal_less_8_out_3), .out_4(bigger_equal_less_8_out_4),
    .out_5(bigger_equal_less_8_out_5));
  not not_8 (not_8_out, bigger_equal_less_8_out_5);
  and and_7 (and_7_out, not_1_out, not_2_out, not_3_out, not_4_out, not_5_out, not_6_out, not_7_out, not_8_out, bigger_equal_less_8_out_3);
  or or_1 (A___B_3, bigger_equal_less_1_out_3, and_1_out, and_2_out, and_3_out, and_4_out, and_5_out, and_6_out, and_7_out);
  not not_9 (not_9_out, A___B_3);
  not not_10 (A____B_3, A___B_3);
  not not_11 (A____B, A___B);
  and and_8 (A___B, bigger_equal_less_8_out_4, bigger_equal_less_7_out_4, bigger_equal_less_6_out_4, bigger_equal_less_5_out_4, bigger_equal_less_4_out_4, bigger_equal_less_3_out_4, bigger_equal_less_2_out_4, bigger_equal_less_1_out_4);
  or or_2 (A____B_2, A___B, A___B_3);
  not not_12 (not_12_out, A___B);
  and and_9 (A___B_2, not_9_out, not_12_out);
endmodule
