// Logisim project cmp.circ as structural Verilog: 49 circuits, main circuit cmp8 unsigned
module cmp8_unsigned (
  input  [7:0] in_1,
  input  [7:0] in_2,
  output out_3,
  output out_4,
  output out_5
);

  wire cmp2_1_1_out_5, cmp2_1_1_out_6, cmp2_1_1_out_7, cmp2_1_out_8, cmp2_1_out_9, cmp2_1_out_10,
       cmp2_3_out_8, cmp2_3_out_9, cmp2_3_out_10;

  cmp2_1 cmp2_1_1 (
    ._0_2(in_2[0]), ._1_2(in_2[1]), ._0(in_1[0]), ._1(in_1[1]), .out_5(cmp2_1_1_out_5),
    .out_6(cmp2_1_1_out_6), .out_7(cmp2_1_1_out_7));
  cmp2 cmp2_1 (
    .in_5(cmp2_1_1_out_5), .in_6(cmp2_1_1_out_6), .in_7(cmp2_1_1_out_7), ._0(in_1[2]), ._1(in_1[3]),
    ._0_2(in_2[2]), ._1_2(in_2[3]), .out_8(cmp2_1_out_8), .out_9(cmp2_1_out_9), .out_10(cmp2_1_out_10));
  cmp2 cmp2_2 (
    .in_5(cmp2_3_out_8), .in_6(cmp2_3_out_9), .in_7(cmp2_3_out_10), ._0(in_1[6]), ._1(in_1[7]),
    ._0_2(in_2[6]), ._1_2(in_2[7]), .out_8(out_3), .out_9(out_4), .out_10(out_5));
  cmp2 cmp2_3 (
    .in_5(cmp2_1_out_8), .in_6(cmp2_1_out_9), .in_7(cmp2_1_out_10), ._0(in_1[4]), ._1(in_1[5]),
    ._0_2(in_2[4]), ._1_2(in_2[5]), .out_8(cmp2_3_out_8), .out_9(cmp2_3_out_9), .out_10(cmp2_3_out_10));
endmodule

module cmp1 (
  input  in_1,
  input  in_2,
  output out_3,
  output out_4,
  output out_5
);

  wire not_1_out, not_2_out, xor_1_out;

  not not_1 (not_1_out, in_1);
  not not_2 (not_2_out, in_2);
  and and_1 (out_3, not_1_out, in_2);
  xor xor_1 (xor_1_out, in_1, in_2);
  and and_2 (out_5, in_1, not_2_out);
  not not_3 (out_4, xor_1_out);
endmodule

module cmp2 (
  input  _0,
  input  _1,
  input  _0_2,
  input  _1_2,
  input  in_5,
  input  in_6,
  input  in_7,
  output out_8,
  output out_9,
  output out_10
);

  wire and_2_out, and_3_out, and_4_out, and_5_out, cmp1_1_out_3, cmp1_1_out_4, cmp1_1_out_5, cmp1_2_out_3,
       cmp1_2_out_4, cmp1_2_out_5;

  cmp1 cmp1_1 (.in_1(_0), .in_2(_0_2), .out_3(cmp1_1_out_3), .out_4(cmp1_1_out_4), .out_5(cmp1_1_out_5));
  cmp1 cmp1_2 (.in_1(_1), .in_2(_1_2), .out_3(cmp1_2_out_3), .out_4(cmp1_2_out_4), .out_5(cmp1_2_out_5));
  and and_1 (out_8, cmp1_2_out_4, cmp1_1_out_4, in_5);
  and and_2 (and_2_out, cmp1_2_out_4, cmp1_1_out_4, in_6);
  and and_3 (and_3_out, cmp1_2_out_4, cmp1_1_out_4, in_7);
  and and_4 (and_4_out, cmp1_1_out_5, cmp1_2_out_4);
  and and_5 (and_5_out, cmp1_1_out_3, cmp1_2_out_4);
  or or_1 (out_9, and_4_out, cmp1_2_out_5, and_2_out);
  or or_2 (out_10, cmp1_2_out_3, and_5_out, and_3_out);

  // Notes on the sheet:
  //   A
  //   B
  //   B
endmodule

module cmp2_1 (
  input  _0,
  input  _1,
  input  _0_2,
  input  _1_2,
  output out_5,
  output out_6,
  output out_7
);

  wire and_1_out, and_2_out, cmp1_1_out_3, cmp1_1_out_4, cmp1_1_out_5, cmp1_2_out_3, cmp1_2_out_4,
       cmp1_2_out_5;

  cmp1 cmp1_1 (.in_1(_0), .in_2(_0_2), .out_3(cmp1_1_out_3), .out_4(cmp1_1_out_4), .out_5(cmp1_1_out_5));
  cmp1 cmp1_2 (.in_1(_1), .in_2(_1_2), .out_3(cmp1_2_out_3), .out_4(cmp1_2_out_4), .out_5(cmp1_2_out_5));
  and and_1 (and_1_out, cmp1_1_out_5, cmp1_2_out_4);
  and and_2 (and_2_out, cmp1_1_out_3, cmp1_2_out_4);
  and and_3 (out_5, cmp1_1_out_4, cmp1_2_out_4);
  or or_1 (out_6, and_1_out, cmp1_2_out_5);
  or or_2 (out_7, and_2_out, cmp1_2_out_3);

  // Notes on the sheet:
  //   B
  //   A
endmodule

module circuit (
  input  [7:0] in_1,
  output [7:0] out_2
);

  assign out_2 = ~in_1;  // NOT_Gate not_1, 8 bits wide
endmodule

module circuit_2 (
  input  [7:0] in_1,
  input  [7:0] in_2,
  output [7:0] out_3
);

  assign out_3 = in_1 & in_2;  // AND_Gate and_1, 8 bits wide
endmodule

module circuit_2_2 (
  input  [7:0] in_1,
  input  [7:0] in_2,
  output [7:0] out_3
);

  assign out_3 = in_1 | in_2;  // OR_Gate or_1, 8 bits wide
endmodule

module circuit_2_2_2 (
  input  [7:0] in_1,
  input  [7:0] in_2,
  output [7:0] out_3
);

  assign out_3 = in_1 ^ in_2;  // XOR_Gate xor_1, 8 bits wide
endmodule

module NOT (
  input  [7:0] in_1,
  output out_2
);

  wire [7:0] part_1_out_2;

  circuit part_1 (.in_1(in_1), .out_2(part_1_out_2));
  and and_1 (out_2, part_1_out_2[0], part_1_out_2[1], part_1_out_2[2], part_1_out_2[3], part_1_out_2[4], part_1_out_2[5], part_1_out_2[6], part_1_out_2[7]);
endmodule

module AND (
  input  [7:0] in_1,
  input  [7:0] in_2,
  output out_3
);

  wire or_1_out, or_2_out;

  or or_1 (or_1_out, in_1[0], in_1[1], in_1[2], in_1[3], in_1[4], in_1[5], in_1[6], in_1[7]);
  or or_2 (or_2_out, in_2[0], in_2[1], in_2[2], in_2[3], in_2[4], in_2[5], in_2[6], in_2[7]);
  and and_1 (out_3, or_1_out, or_2_out);
endmodule

module OR (
  input  [7:0] in_1,
  input  [7:0] in_2,
  output out_3
);

  wire or_1_out, or_2_out;

  or or_1 (or_1_out, in_1[0], in_1[1], in_1[2], in_1[3], in_1[4], in_1[5], in_1[6], in_1[7]);
  or or_2 (or_2_out, in_2[0], in_2[1], in_2[2], in_2[3], in_2[4], in_2[5], in_2[6], in_2[7]);
  or or_3 (out_3, or_1_out, or_2_out);
endmodule

module XOR (
  input  [7:0] in_1,
  input  [7:0] in_2,
  output out_3
);

  wire or_1_out, or_2_out;

  or or_1 (or_1_out, in_1[0], in_1[1], in_1[2], in_1[3], in_1[4], in_1[5], in_1[6], in_1[7]);
  or or_2 (or_2_out, in_2[0], in_2[1], in_2[2], in_2[3], in_2[4], in_2[5], in_2[6], in_2[7]);
  xor xor_1 (out_3, or_1_out, or_2_out);
endmodule

module \unsigned  (
  input  [7:0] in_1,
  input  [7:0] in_2,
  output out_3
);

  cmp8_unsigned cmp8_unsigned_1 (.in_1(in_1), .in_2(in_2), .out_3(out_3));  // open: out_4, out_5
endmodule

module unsigned_2 (
  input  [7:0] in_1,
  input  [7:0] in_2,
  output out_3
);

  wire cmp8_unsigned_1_out_3;

  cmp8_unsigned cmp8_unsigned_1 (.in_1(in_1), .in_2(in_2), .out_3(cmp8_unsigned_1_out_3));  // open: out_4, out_5
  not not_1 (out_3, cmp8_unsigned_1_out_3);
endmodule

module S_ADD (
  input  A,
  input  B,
  output Y,
  output S
);

  and and_1 (S, A, B);
  xor xor_1 (Y, A, B);
endmodule

module unsigned_2_2 (
  input  [7:0] in_1,
  input  [7:0] in_2,
  output out_3
);

  cmp8_unsigned cmp8_unsigned_1 (.in_1(in_1), .in_2(in_2), .out_4(out_3));  // open: out_3, out_5
endmodule

module unsigned_2_2_2 (
  input  [7:0] in_1,
  input  [7:0] in_2,
  output out_3
);

  cmp8_unsigned cmp8_unsigned_1 (.in_1(in_1), .in_2(in_2), .out_5(out_3));  // open: out_3, out_4
endmodule

module unsigned_2_2_2_2 (
  input  [7:0] in_1,
  input  [7:0] in_2,
  output out_3
);

  wire cmp8_unsigned_1_out_4;

  cmp8_unsigned cmp8_unsigned_1 (.in_1(in_1), .in_2(in_2), .out_4(cmp8_unsigned_1_out_4));  // open: out_3, out_5
  not not_1 (out_3, cmp8_unsigned_1_out_4);
endmodule

module unsigned_2_2_2_2_2 (
  input  [7:0] in_1,
  input  [7:0] in_2,
  output out_3
);

  wire cmp8_unsigned_1_out_5;

  not not_1 (out_3, cmp8_unsigned_1_out_5);
  cmp8_unsigned cmp8_unsigned_1 (.in_1(in_1), .in_2(in_2), .out_5(cmp8_unsigned_1_out_5));  // open: out_3, out_4
endmodule

module ADD (
  input  S1,
  input  A,
  input  B,
  output Y,
  output S2
);

  wire and_1_out, s_add_1_s, s_add_1_y;

  S_ADD s_add_1 (.A(A), .B(B), .Y(s_add_1_y), .S(s_add_1_s));
  and and_1 (and_1_out, S1, s_add_1_y);
  xor xor_1 (Y, S1, s_add_1_y);
  or or_1 (S2, s_add_1_s, and_1_out);
endmodule

module add8_unsingned (
  input  [7:0] in_1,
  input  [7:0] in_2,
  output [7:0] out_3,
  output S
);

  wire add_1_s2, add_2_s2, add_3_s2, add_4_s2, add_5_s2, add_6_s2, s_add_1_s;

  S_ADD s_add_1 (.A(in_1[0]), .B(in_2[0]), .Y(out_3[0]), .S(s_add_1_s));
  ADD add_1 (.A(in_1[1]), .B(in_2[1]), .S1(s_add_1_s), .Y(out_3[1]), .S2(add_1_s2));
  ADD add_2 (.A(in_1[2]), .B(in_2[2]), .S1(add_1_s2), .Y(out_3[2]), .S2(add_2_s2));
  ADD add_3 (.A(in_1[3]), .B(in_2[3]), .S1(add_2_s2), .Y(out_3[3]), .S2(add_3_s2));
  ADD add_4 (.A(in_1[4]), .B(in_2[4]), .S1(add_3_s2), .Y(out_3[4]), .S2(add_4_s2));
  ADD add_5 (.A(in_1[5]), .B(in_2[5]), .S1(add_4_s2), .Y(out_3[5]), .S2(add_5_s2));
  ADD add_6 (.A(in_1[6]), .B(in_2[6]), .S1(add_5_s2), .Y(out_3[6]), .S2(add_6_s2));
  ADD add_7 (.A(in_1[7]), .B(in_2[7]), .S1(add_6_s2), .Y(out_3[7]), .S2(S));
endmodule

module logic____1 (
  input  [7:0] in_1,
  output [7:0] out_2
);


  assign out_2 = {1'b0, in_1[7:1]};
endmodule

module shifter_8 (
  input  [7:0] in_1,
  input  [2:0] shift,
  input  [2:0] Code,
  output [7:0] out_4
);

  wire [7:0] arith_1_1_out_2, arith_1_2_out_2, arith_1_3_out_2, arith_1_4_out_2, arith_1_5_out_2,
       arith_1_6_out_2, arith_1_7_out_2, circ_1_1_out_2, circ_1_2_out_2, circ_1_3_out_2, circ_1_4_out_2,
       circ_1_5_out_2, circ_1_6_out_2, circ_1_7_out_2, circl_1_1_out_2, circl_1_2_out_2, circl_1_3_out_2,
       circl_1_4_out_2, circl_1_5_out_2, circl_1_6_out_2, circl_1_7_out_2, log_1_1_out_2, log_1_2_out_2,
       log_1_3_out_2, log_1_4_out_2, log_1_5_out_2, log_1_6_out_2, log_1_7_out_2, logic_1_1_out_2,
       logic_1_2_out_2, logic_1_3_out_2, logic_1_4_out_2, logic_1_5_out_2, logic_1_6_out_2, logic_1_7_out_2,
       multiplexer_1_out, multiplexer_2_out, multiplexer_3_out, multiplexer_4_out, multiplexer_5_out;

  logic____1 logic_1_1 (.in_1(in_1), .out_2(logic_1_1_out_2));
  log____1 log_1_1 (.in_1(in_1), .out_2(log_1_1_out_2));
  Multiplexer #(.select(3), .width(8)) multiplexer_1 (
    .in0(logic_1_1_out_2), .in1(log_1_1_out_2), .in2(arith_1_1_out_2), .in3(circl_1_1_out_2),
    .in4(circ_1_1_out_2), .out(multiplexer_1_out), .sel(Code));  // open: in5, in6, in7, en
  arith____1 arith_1_1 (.in_1(in_1), .out_2(arith_1_1_out_2));
  circl____1 circl_1_1 (.in_1(in_1), .out_2(circl_1_1_out_2));
  circ____1 circ_1_1 (.in_1(in_1), .out_2(circ_1_1_out_2));
  Multiplexer #(.width(8)) multiplexer_2 (
    .in0(in_1), .in1(multiplexer_1_out), .out(multiplexer_2_out), .sel(shift[0]));  // open: en
  logic____1 logic_1_2 (.in_1(multiplexer_2_out), .out_2(logic_1_2_out_2));
  log____1 log_1_2 (.in_1(multiplexer_2_out), .out_2(log_1_2_out_2));
  arith____1 arith_1_2 (.in_1(multiplexer_2_out), .out_2(arith_1_2_out_2));
  circl____1 circl_1_2 (.in_1(multiplexer_2_out), .out_2(circl_1_2_out_2));
  circ____1 circ_1_2 (.in_1(multiplexer_2_out), .out_2(circ_1_2_out_2));
  logic____1 logic_1_3 (.in_1(logic_1_2_out_2), .out_2(logic_1_3_out_2));
  log____1 log_1_3 (.in_1(log_1_2_out_2), .out_2(log_1_3_out_2));
  arith____1 arith_1_3 (.in_1(arith_1_2_out_2), .out_2(arith_1_3_out_2));
  circl____1 circl_1_3 (.in_1(circl_1_2_out_2), .out_2(circl_1_3_out_2));
  circ____1 circ_1_3 (.in_1(circ_1_2_out_2), .out_2(circ_1_3_out_2));
  Multiplexer #(.width(8)) multiplexer_3 (
    .in0(multiplexer_2_out), .in1(multiplexer_4_out), .out(multiplexer_3_out), .sel(shift[1]));  // open: en
  Multiplexer #(.select(3), .width(8)) multiplexer_4 (
    .in0(logic_1_3_out_2), .in1(log_1_3_out_2), .in2(arith_1_3_out_2), .in3(circl_1_3_out_2),
    .in4(circ_1_3_out_2), .in5(circ_1_3_out_2), .out(multiplexer_4_out), .sel(Code));  // open: in6, in7, en
  logic____1 logic_1_4 (.in_1(multiplexer_3_out), .out_2(logic_1_4_out_2));
  log____1 log_1_4 (.in_1(multiplexer_3_out), .out_2(log_1_4_out_2));
  arith____1 arith_1_4 (.in_1(multiplexer_3_out), .out_2(arith_1_4_out_2));
  circl____1 circl_1_4 (.in_1(multiplexer_3_out), .out_2(circl_1_4_out_2));
  circ____1 circ_1_4 (.in_1(multiplexer_3_out), .out_2(circ_1_4_out_2));
  logic____1 logic_1_5 (.in_1(logic_1_4_out_2), .out_2(logic_1_5_out_2));
  logic____1 logic_1_6 (.in_1(logic_1_5_out_2), .out_2(logic_1_6_out_2));
  log____1 log_1_5 (.in_1(log_1_6_out_2), .out_2(log_1_5_out_2));
  log____1 log_1_6 (.in_1(log_1_4_out_2), .out_2(log_1_6_out_2));
  arith____1 arith_1_5 (.in_1(arith_1_6_out_2), .out_2(arith_1_5_out_2));
  arith____1 arith_1_6 (.in_1(arith_1_4_out_2), .out_2(arith_1_6_out_2));
  circl____1 circl_1_5 (.in_1(circl_1_4_out_2), .out_2(circl_1_5_out_2));
  circl____1 circl_1_6 (.in_1(circl_1_5_out_2), .out_2(circl_1_6_out_2));
  circ____1 circ_1_5 (.in_1(circ_1_4_out_2), .out_2(circ_1_5_out_2));
  circ____1 circ_1_6 (.in_1(circ_1_5_out_2), .out_2(circ_1_6_out_2));
  logic____1 logic_1_7 (.in_1(logic_1_6_out_2), .out_2(logic_1_7_out_2));
  log____1 log_1_7 (.in_1(log_1_5_out_2), .out_2(log_1_7_out_2));
  arith____1 arith_1_7 (.in_1(arith_1_5_out_2), .out_2(arith_1_7_out_2));
  circl____1 circl_1_7 (.in_1(circl_1_6_out_2), .out_2(circl_1_7_out_2));
  circ____1 circ_1_7 (.in_1(circ_1_6_out_2), .out_2(circ_1_7_out_2));
  Multiplexer #(.select(3), .width(8)) multiplexer_5 (
    .in0(logic_1_7_out_2), .in1(log_1_7_out_2), .in2(arith_1_7_out_2), .in3(circl_1_7_out_2),
    .in4(circ_1_7_out_2), .out(multiplexer_5_out), .sel(Code));  // open: in5, in6, in7, en
  Multiplexer #(.width(8)) multiplexer_6 (
    .in0(multiplexer_3_out), .in1(multiplexer_5_out), .out(out_4), .sel(shift[2]));  // open: en
endmodule

module log____1 (
  input  [7:0] in_1,
  output [7:0] out_2
);


  assign out_2 = {in_1[6:0], 1'b0};
endmodule

module arith____1 (
  input  [7:0] in_1,
  output [7:0] out_2
);


  assign out_2 = {{2{in_1[7]}}, in_1[6:1]};
endmodule

module circl____1 (
  input  [7:0] in_1,
  output [7:0] out_2
);


  assign out_2 = {in_1[0], in_1[7:1]};
endmodule

module circ____1 (
  input  [7:0] in_1,
  output [7:0] out_2
);


  assign out_2 = {in_1[6:0], in_1[7]};
endmodule

module cmp8_signed (
  input  [7:0] in_1,
  input  [7:0] in_2,
  output out_3,
  output out_4,
  output out_5
);

  wire [7:0] xor_1_out, xor_2_out;

  assign xor_1_out = in_1 ^ 8'h80;  // XOR_Gate xor_1, 8 bits wide
  assign xor_2_out = 8'h80 ^ in_2;  // XOR_Gate xor_2, 8 bits wide
  cmp8_unsigned cmp8_unsigned_1 (.in_1(xor_1_out), .in_2(xor_2_out), .out_3(out_3), .out_4(out_4), .out_5(out_5));
endmodule

module \signed  (
  input  [7:0] in_1,
  input  [7:0] in_2,
  output out_3
);

  cmp8_signed cmp8_signed_1 (.in_1(in_1), .in_2(in_2), .out_3(out_3));  // open: out_4, out_5
endmodule

module signed_2 (
  input  [7:0] in_1,
  input  [7:0] in_2,
  output out_3
);

  cmp8_signed cmp8_signed_1 (.in_1(in_1), .in_2(in_2), .out_4(out_3));  // open: out_3, out_5
endmodule

module signed_2_2 (
  input  [7:0] in_1,
  input  [7:0] in_2,
  output out_3
);

  cmp8_signed cmp8_signed_1 (.in_1(in_1), .in_2(in_2), .out_5(out_3));  // open: out_3, out_4
endmodule

module signed_2_2_2 (
  input  [7:0] in_1,
  input  [7:0] in_2,
  output out_3
);

  wire cmp8_signed_1_out_3;

  cmp8_signed cmp8_signed_1 (.in_1(in_1), .in_2(in_2), .out_3(cmp8_signed_1_out_3));  // open: out_4, out_5
  not not_1 (out_3, cmp8_signed_1_out_3);
endmodule

module signed_2_2_2_2 (
  input  [7:0] in_1,
  input  [7:0] in_2,
  output out_3
);

  wire cmp8_signed_1_out_4;

  not not_1 (out_3, cmp8_signed_1_out_4);
  cmp8_signed cmp8_signed_1 (.in_1(in_1), .in_2(in_2), .out_4(cmp8_signed_1_out_4));  // open: out_3, out_5
endmodule

module signed_2_2_2_2_2 (
  input  [7:0] in_1,
  input  [7:0] in_2,
  output out_3
);

  wire cmp8_signed_1_out_5;

  cmp8_signed cmp8_signed_1 (.in_1(in_1), .in_2(in_2), .out_5(cmp8_signed_1_out_5));  // open: out_3, out_4
  not not_1 (out_3, cmp8_signed_1_out_5);
endmodule

module sub8_unsigned (
  input  [7:0] in_1,
  input  [7:0] in_2,
  output [7:0] out_3,
  output S
);

  wire add_1_s2, add_2_s2, add_3_s2, add_4_s2, add_5_s2, add_6_s2, add_7_s2, add_8_s2;
  wire [7:0] not_1_out;

  assign not_1_out = ~in_2;  // NOT_Gate not_1, 8 bits wide
  ADD add_1 (.A(in_1[0]), .B(not_1_out[0]), .S1(1'b1), .Y(out_3[0]), .S2(add_1_s2));
  ADD add_2 (.A(in_1[1]), .B(not_1_out[1]), .S1(add_1_s2), .Y(out_3[1]), .S2(add_2_s2));
  ADD add_3 (.A(in_1[2]), .B(not_1_out[2]), .S1(add_2_s2), .Y(out_3[2]), .S2(add_3_s2));
  ADD add_4 (.A(in_1[3]), .B(not_1_out[3]), .S1(add_3_s2), .Y(out_3[3]), .S2(add_4_s2));
  ADD add_5 (.A(in_1[4]), .B(not_1_out[4]), .S1(add_4_s2), .Y(out_3[4]), .S2(add_5_s2));
  ADD add_6 (.A(in_1[5]), .B(not_1_out[5]), .S1(add_5_s2), .Y(out_3[5]), .S2(add_6_s2));
  ADD add_7 (.A(in_1[6]), .B(not_1_out[6]), .S1(add_6_s2), .Y(out_3[6]), .S2(add_7_s2));
  ADD add_8 (.A(in_1[7]), .B(not_1_out[7]), .S1(add_7_s2), .Y(out_3[7]), .S2(add_8_s2));
  not not_2 (S, add_8_s2);
endmodule

module mul4_unsigned (
  input  [3:0] D,
  input  [3:0] \С ,
  input  [3:0] in_3,
  input  [3:0] in_4,
  output [3:0] out_5,
  output [3:0] out_6
);

  wire add_1_s2, add_1_y, add_2_s2, add_2_y, add_3_s2, add_3_y, add_4_s2, add_4_y, add_5_s2, add_5_y,
       add_6_s2, add_6_y, add_7_s2, add_7_y, add_8_s2, add_8_y, add_9_s2, add_9_y, add_10_s2, add_11_s2,
       add_12_s2, add_13_s2, add_14_s2, add_15_s2, and_1_out, and_2_out, and_3_out, and_4_out, and_5_out,
       and_6_out, and_7_out, and_8_out, and_9_out, and_10_out, and_11_out, and_12_out, and_13_out,
       and_14_out, and_15_out, and_16_out;

  and and_1 (and_1_out, in_3[0], in_4[0]);
  and and_2 (and_2_out, in_3[1], in_4[0]);
  and and_3 (and_3_out, in_3[0], in_4[1]);
  and and_4 (and_4_out, in_3[1], in_4[1]);
  and and_5 (and_5_out, in_3[2], in_4[0]);
  and and_6 (and_6_out, in_4[0], in_3[3]);
  and and_7 (and_7_out, in_4[1], in_3[2]);
  and and_8 (and_8_out, in_3[1], in_4[2]);
  and and_9 (and_9_out, in_3[3], in_4[1]);
  and and_10 (and_10_out, in_3[3], in_4[2]);
  and and_11 (and_11_out, in_3[2], in_4[3]);
  and and_12 (and_12_out, in_3[3], in_4[3]);
  ADD add_1 (.A(and_2_out), .B(and_3_out), .S1(\С [1]), .Y(add_1_y), .S2(add_1_s2));
  and and_13 (and_13_out, in_3[0], in_4[2]);
  and and_14 (and_14_out, in_3[0], in_4[3]);
  and and_15 (and_15_out, in_3[2], in_4[2]);
  and and_16 (and_16_out, in_4[3], in_3[1]);
  ADD add_2 (.A(and_4_out), .B(and_5_out), .S1(\С [2]), .Y(add_2_y), .S2(add_2_s2));
  ADD add_3 (.A(and_6_out), .B(and_7_out), .S1(\С [3]), .Y(add_3_y), .S2(add_3_s2));
  ADD add_4 (.A(and_9_out), .B(and_15_out), .S1(add_3_s2), .Y(add_4_y), .S2(add_4_s2));
  ADD add_5 (.A(add_2_y), .B(add_1_s2), .S1(and_13_out), .Y(add_5_y), .S2(add_5_s2));
  ADD add_6 (.A(add_3_y), .B(and_8_out), .S1(add_2_s2), .Y(add_6_y), .S2(add_6_s2));
  ADD add_7 (.A(add_4_y), .B(and_16_out), .S1(add_6_s2), .Y(add_7_y), .S2(add_7_s2));
  ADD add_8 (.A(and_10_out), .B(and_11_out), .S1(add_4_s2), .Y(add_8_y), .S2(add_8_s2));
  ADD add_9 (.A(add_6_y), .B(and_14_out), .S1(add_5_s2), .Y(add_9_y), .S2(add_9_s2));
  ADD add_10 (.A(and_1_out), .B(\С [0]), .S1(D[0]), .Y(out_5[0]), .S2(add_10_s2));
  ADD add_11 (.A(D[1]), .B(add_1_y), .S1(add_10_s2), .Y(out_5[1]), .S2(add_11_s2));
  ADD add_12 (.A(add_5_y), .B(D[2]), .S1(add_11_s2), .Y(out_5[2]), .S2(add_12_s2));
  ADD add_13 (.A(D[3]), .B(add_9_y), .S1(add_12_s2), .Y(out_5[3]), .S2(add_13_s2));
  ADD add_14 (.A(add_7_s2), .B(add_8_y), .S1(add_15_s2), .Y(out_6[1]), .S2(add_14_s2));
  ADD add_15 (.A(add_9_s2), .B(add_7_y), .S1(add_13_s2), .Y(out_6[0]), .S2(add_15_s2));
  ADD add_16 (.A(add_8_s2), .B(and_12_out), .S1(add_14_s2), .Y(out_6[2]), .S2(out_6[3]));
endmodule

module mul8_unsigned (
  input  [7:0] A,
  input  [7:0] B,
  output [7:0] M,
  output [7:0] C
);

  wire [3:0] mul4_unsigned_1_out_5, mul4_unsigned_1_out_6, mul4_unsigned_2_out_6, mul4_unsigned_3_out_6;

  mul4_unsigned mul4_unsigned_1 (
    .in_3(A[3:0]), .in_4(B[7:4]), .\С (4'b0000), .D(4'b0000), .out_5(mul4_unsigned_1_out_5),
    .out_6(mul4_unsigned_1_out_6));
  mul4_unsigned mul4_unsigned_2 (
    .in_3(A[3:0]), .in_4(B[3:0]), .\С (4'b0000), .D(4'b0000), .out_5(M[3:0]), .out_6(mul4_unsigned_2_out_6));
  mul4_unsigned mul4_unsigned_3 (
    .in_3(A[7:4]), .in_4(B[3:0]), .\С (mul4_unsigned_2_out_6), .D(mul4_unsigned_1_out_5), .out_5(M[7:4]),
    .out_6(mul4_unsigned_3_out_6));
  mul4_unsigned mul4_unsigned_4 (
    .in_3(A[7:4]), .in_4(B[7:4]), .\С (mul4_unsigned_1_out_6), .D(mul4_unsigned_3_out_6), .out_5(C[3:0]),
    .out_6(C[7:4]));
endmodule

module dev8_unsigned (
  input  [7:0] A,
  input  [7:0] D,
  output [7:0] Q,
  output Err
);

  wire not_2_out_2, not_3_out_2, not_4_out_2, not_5_out_2, not_6_out_2, not_7_out_2, not_8_out_2,
       not_9_out_2, unsigned_1_out_3, unsigned_2_out_3, unsigned_3_out_3, unsigned_4_out_3, unsigned_5_out_3,
       unsigned_6_out_3, unsigned_7_out_3, unsigned_8_out_3;
  wire [7:0] multiplier_1_cout, multiplier_1_out, multiplier_2_cout, multiplier_2_out, multiplier_3_cout,
       multiplier_3_out, multiplier_4_cout, multiplier_4_out, multiplier_5_cout, multiplier_5_out,
       multiplier_6_cout, multiplier_6_out, multiplier_7_cout, multiplier_7_out, multiplier_8_cout,
       multiplier_8_out;

  NOT not_1 (.in_1(D), .out_2(Err));
  unsigned_2_2_2_2_2 unsigned_1 (.in_1(A), .in_2(multiplier_1_out), .out_3(unsigned_1_out_3));
  Multiplier multiplier_1 (.a(D), .b(8'h80), .out(multiplier_1_out), .cout(multiplier_1_cout));  // open: cin
  and and_1 (Q[7], unsigned_1_out_3, not_2_out_2);
  NOT not_2 (.in_1(multiplier_1_cout), .out_2(not_2_out_2));
  unsigned_2_2_2_2_2 unsigned_2 (.in_1(A), .in_2(multiplier_2_out), .out_3(unsigned_2_out_3));
  Multiplier multiplier_2 (
    .a(D), .b({Q[7], 7'b1000000}), .out(multiplier_2_out), .cout(multiplier_2_cout));  // open: cin
  and and_2 (Q[6], unsigned_2_out_3, not_3_out_2);
  NOT not_3 (.in_1(multiplier_2_cout), .out_2(not_3_out_2));
  Multiplier multiplier_3 (
    .a(D), .b({Q[7:6], 6'b100000}), .out(multiplier_3_out), .cout(multiplier_3_cout));  // open: cin
  NOT not_4 (.in_1(multiplier_3_cout), .out_2(not_4_out_2));
  and and_3 (Q[5], not_4_out_2, unsigned_3_out_3);
  unsigned_2_2_2_2_2 unsigned_3 (.in_1(A), .in_2(multiplier_3_out), .out_3(unsigned_3_out_3));
  unsigned_2_2_2_2_2 unsigned_4 (.in_1(A), .in_2(multiplier_4_out), .out_3(unsigned_4_out_3));
  NOT not_5 (.in_1(multiplier_4_cout), .out_2(not_5_out_2));
  Multiplier multiplier_4 (
    .a(D), .b({Q[7:5], 5'b10000}), .out(multiplier_4_out), .cout(multiplier_4_cout));  // open: cin
  and and_4 (Q[4], unsigned_4_out_3, not_5_out_2);
  unsigned_2_2_2_2_2 unsigned_5 (.in_1(A), .in_2(multiplier_5_out), .out_3(unsigned_5_out_3));
  Multiplier multiplier_5 (
    .a(D), .b({Q[7:4], 4'b1000}), .out(multiplier_5_out), .cout(multiplier_5_cout));  // open: cin
  and and_5 (Q[3], unsigned_5_out_3, not_6_out_2);
  NOT not_6 (.in_1(multiplier_5_cout), .out_2(not_6_out_2));
  Multiplier multiplier_6 (.a(D), .b({Q[7:3], 3'b100}), .out(multiplier_6_out), .cout(multiplier_6_cout));  // open: cin
  unsigned_2_2_2_2_2 unsigned_6 (.in_1(A), .in_2(multiplier_6_out), .out_3(unsigned_6_out_3));
  Multiplier multiplier_7 (.a(D), .b({Q[7:2], 2'b10}), .out(multiplier_7_out), .cout(multiplier_7_cout));  // open: cin
  and and_6 (Q[2], unsigned_6_out_3, not_7_out_2);
  NOT not_7 (.in_1(multiplier_6_cout), .out_2(not_7_out_2));
  unsigned_2_2_2_2_2 unsigned_7 (.in_1(A), .in_2(multiplier_7_out), .out_3(unsigned_7_out_3));
  and and_7 (Q[1], unsigned_7_out_3, not_8_out_2);
  NOT not_8 (.in_1(multiplier_7_cout), .out_2(not_8_out_2));
  Multiplier multiplier_8 (.a(D), .b({Q[7:1], 1'b1}), .out(multiplier_8_out), .cout(multiplier_8_cout));  // open: cin
  unsigned_2_2_2_2_2 unsigned_8 (.in_1(A), .in_2(multiplier_8_out), .out_3(unsigned_8_out_3));
  NOT not_9 (.in_1(multiplier_8_cout), .out_2(not_9_out_2));
  and and_8 (Q[0], unsigned_8_out_3, not_9_out_2);
endmodule

module mod8_unsigned (
  input  [7:0] A,
  input  [7:0] D,
  output [7:0] R,
  output Err
);

  wire [7:0] dev8_unsigned_1_q, multiplier_1_out;

  dev8_unsigned dev8_unsigned_1 (.A(A), .D(D), .Err(Err), .Q(dev8_unsigned_1_q));
  Multiplier multiplier_1 (.a(D), .b(dev8_unsigned_1_q), .out(multiplier_1_out));  // open: cin, cout
  sub8_unsigned sub8_unsigned_1 (.in_1(A), .in_2(multiplier_1_out), .out_3(R));  // open: S
endmodule

module sub8_signed (
  input  [7:0] in_1,
  input  [7:0] in_2,
  output [7:0] out_3,
  output S
);

  wire add_1_s2, add_2_s2, add_3_s2, add_4_s2, add_5_s2, add_6_s2, add_7_s2, add_8_s2;
  wire [7:0] not_1_out;

  assign not_1_out = ~in_2;  // NOT_Gate not_1, 8 bits wide
  ADD add_1 (.A(in_1[0]), .B(not_1_out[0]), .S1(1'b1), .Y(out_3[0]), .S2(add_1_s2));
  ADD add_2 (.A(in_1[1]), .B(not_1_out[1]), .S1(add_1_s2), .Y(out_3[1]), .S2(add_2_s2));
  ADD add_3 (.A(in_1[2]), .B(not_1_out[2]), .S1(add_2_s2), .Y(out_3[2]), .S2(add_3_s2));
  ADD add_4 (.A(in_1[3]), .B(not_1_out[3]), .S1(add_3_s2), .Y(out_3[3]), .S2(add_4_s2));
  ADD add_5 (.A(in_1[4]), .B(not_1_out[4]), .S1(add_4_s2), .Y(out_3[4]), .S2(add_5_s2));
  ADD add_6 (.A(in_1[5]), .B(not_1_out[5]), .S1(add_5_s2), .Y(out_3[5]), .S2(add_6_s2));
  ADD add_7 (.A(in_1[6]), .B(not_1_out[6]), .S1(add_6_s2), .Y(out_3[6]), .S2(add_7_s2));
  ADD add_8 (.A(in_1[7]), .B(not_1_out[7]), .S1(add_7_s2), .Y(out_3[7]), .S2(add_8_s2));
  not not_2 (S, add_8_s2);
endmodule

module add_signed (
  input  [7:0] in_1,
  input  [7:0] in_2,
  output [7:0] out_3,
  output S
);

  wire add_1_s2, add_2_s2, add_3_s2, add_4_s2, add_5_s2, add_6_s2, add_7_s2, s_add_1_s;

  S_ADD s_add_1 (.A(in_1[0]), .B(in_2[0]), .Y(out_3[0]), .S(s_add_1_s));
  ADD add_1 (.A(in_1[1]), .B(in_2[1]), .S1(s_add_1_s), .Y(out_3[1]), .S2(add_1_s2));
  ADD add_2 (.A(in_1[2]), .B(in_2[2]), .S1(add_1_s2), .Y(out_3[2]), .S2(add_2_s2));
  ADD add_3 (.A(in_1[3]), .B(in_2[3]), .S1(add_2_s2), .Y(out_3[3]), .S2(add_3_s2));
  ADD add_4 (.A(in_1[4]), .B(in_2[4]), .S1(add_3_s2), .Y(out_3[4]), .S2(add_4_s2));
  ADD add_5 (.A(in_1[5]), .B(in_2[5]), .S1(add_4_s2), .Y(out_3[5]), .S2(add_5_s2));
  ADD add_6 (.A(in_1[6]), .B(in_2[6]), .S1(add_5_s2), .Y(out_3[6]), .S2(add_6_s2));
  ADD add_7 (.A(in_1[7]), .B(in_2[7]), .S1(add_6_s2), .Y(out_3[7]), .S2(add_7_s2));
  xor xor_1 (S, add_6_s2, add_7_s2);
endmodule

module mul8_signed (
  input  [7:0] in_1,
  input  [7:0] in_2,
  output [7:0] R,
  output [7:0] R_2
);

  wire xor_1_out;
  wire [7:0] convert_straight_1_out_2, convert_straight_2_out_2, multiplier_1_cout, multiplier_1_out;
  wire [15:0] adder_1_out, not_1_out;

  convert_straight convert_straight_1 (.in_1(in_1), .out_2(convert_straight_1_out_2));
  convert_straight convert_straight_2 (.in_1(in_2), .out_2(convert_straight_2_out_2));
  xor xor_1 (xor_1_out, in_1[7], in_2[7]);
  Multiplier multiplier_1 (
    .a(convert_straight_1_out_2), .b(convert_straight_2_out_2), .out(multiplier_1_out),
    .cout(multiplier_1_cout));  // open: cin
  assign not_1_out = ~{multiplier_1_cout, multiplier_1_out};  // NOT_Gate not_1, 16 bits wide
  Multiplexer #(.width(16)) multiplexer_1 (
    .in0({multiplier_1_cout, multiplier_1_out}), .in1(adder_1_out), .out({R_2, R}), .sel(xor_1_out));  // open: en
  Adder #(.width(16)) adder_1 (.a(not_1_out), .b(16'h1), .out(adder_1_out));  // open: cin, cout
endmodule

module dev8_signed (
  input  [7:0] in_1,
  input  [7:0] in_2,
  output [7:0] R
);

  wire xor_1_out;
  wire [7:0] adder_1_out, convert_straight_1_out_2, convert_straight_2_out_2, dev8_unsigned_1_q, not_1_out;

  convert_straight convert_straight_1 (.in_1(in_1), .out_2(convert_straight_1_out_2));
  convert_straight convert_straight_2 (.in_1(in_2), .out_2(convert_straight_2_out_2));
  xor xor_1 (xor_1_out, in_1[7], in_2[7]);
  dev8_unsigned dev8_unsigned_1 (
    .A(convert_straight_1_out_2), .D(convert_straight_2_out_2), .Q(dev8_unsigned_1_q));  // open: Err
  assign not_1_out = ~dev8_unsigned_1_q;  // NOT_Gate not_1, 8 bits wide
  Multiplexer #(.width(8)) multiplexer_1 (
    .in0(dev8_unsigned_1_q), .in1(adder_1_out), .out(R), .sel(xor_1_out));  // open: en
  Adder adder_1 (.a(not_1_out), .b(8'h1), .out(adder_1_out));  // open: cin, cout
endmodule

module alu (
  input  [7:0] _1,
  input  [7:0] _2,
  input  [3:0] \Код ,
  output [7:0] R
);

  wire [1:0] demultiplexer_2_out8_3;
  wire [2:0] demultiplexer_2_out7, demultiplexer_2_out8, demultiplexer_2_out8_2;
  wire [7:0] add8_unsingned_1_out_3, demultiplexer_1_out0, demultiplexer_1_out1, demultiplexer_1_out2,
       demultiplexer_1_out3, demultiplexer_1_out4, demultiplexer_1_out5, demultiplexer_1_out6,
       demultiplexer_1_out7, demultiplexer_1_out8, demultiplexer_1_out9, demultiplexer_2_out0,
       demultiplexer_2_out1, demultiplexer_2_out2, demultiplexer_2_out3, demultiplexer_2_out4,
       demultiplexer_2_out5, demultiplexer_2_out6, demultiplexer_2_out9, dev8_unsigned_1_q,
       mod8_unsigned_1_r, mul8_unsigned_1_m, shifter_8_1_out_4, shifter_8_2_out_4, shifter_8_3_out_4,
       shifter_8_4_out_4, sub8_unsigned_1_out_3;
  wire [7:3] demultiplexer_2_out7_2;

  Demultiplexer #(.select(4), .width(8)) demultiplexer_1 (
    .out0(demultiplexer_1_out0), .out1(demultiplexer_1_out1), .out2(demultiplexer_1_out2),
    .out3(demultiplexer_1_out3), .out4(demultiplexer_1_out4), .out5(demultiplexer_1_out5),
    .out6(demultiplexer_1_out6), .out7(demultiplexer_1_out7), .out8(demultiplexer_1_out8),
    .out9(demultiplexer_1_out9), .in(_1), .sel(\Код ));  // open: out10, out11, out12, out13, out14, out15, en
  Demultiplexer #(.select(4), .width(8)) demultiplexer_2 (
    .out0(demultiplexer_2_out0), .out1(demultiplexer_2_out1), .out2(demultiplexer_2_out2),
    .out3(demultiplexer_2_out3), .out4(demultiplexer_2_out4), .out5(demultiplexer_2_out5),
    .out6(demultiplexer_2_out6), .out7({demultiplexer_2_out7_2, demultiplexer_2_out7}),
    .out8({demultiplexer_2_out8_3, demultiplexer_2_out8_2, demultiplexer_2_out8}),
    .out9(demultiplexer_2_out9), .in(_2), .sel(\Код ));  // open: out10, out11, out12, out13, out14, out15, en
  add8_unsingned add8_unsingned_1 (
    .in_1(demultiplexer_1_out0), .in_2(demultiplexer_2_out0), .out_3(add8_unsingned_1_out_3));  // open: S
  sub8_unsigned sub8_unsigned_1 (
    .in_1(demultiplexer_1_out1), .in_2(demultiplexer_2_out1), .out_3(sub8_unsigned_1_out_3));  // open: S
  mul8_unsigned mul8_unsigned_1 (.A(demultiplexer_1_out2), .B(demultiplexer_2_out2), .M(mul8_unsigned_1_m));  // open: C
  dev8_unsigned dev8_unsigned_1 (
    .A(demultiplexer_1_out3), .D(demultiplexer_2_out3), .Q(dev8_unsigned_1_q));  // open: Err
  mod8_unsigned mod8_unsigned_1 (
    .A(demultiplexer_1_out4), .D(demultiplexer_2_out4), .R(mod8_unsigned_1_r));  // open: Err
  shifter_8 shifter_8_1 (
    .in_1(demultiplexer_1_out5), .shift(demultiplexer_2_out5[2:0]), .Code(3'b000), .out_4(shifter_8_1_out_4));
  shifter_8 shifter_8_2 (
    .in_1(demultiplexer_1_out6), .shift(demultiplexer_2_out6[2:0]), .Code(3'b001), .out_4(shifter_8_2_out_4));
  shifter_8 shifter_8_3 (
    .in_1(demultiplexer_1_out7), .shift(demultiplexer_2_out7), .Code(3'b011), .out_4(shifter_8_3_out_4));
  shifter_8 shifter_8_4 (
    .in_1(demultiplexer_1_out8), .shift(demultiplexer_2_out8), .Code(3'b100), .out_4(shifter_8_4_out_4));
  cmp8_unsigned cmp8_unsigned_1 (
    .in_1(demultiplexer_1_out9), .in_2(demultiplexer_2_out9));  // open: out_3, out_4, out_5
  Multiplexer #(.select(4), .width(8)) multiplexer_1 (
    .in0(add8_unsingned_1_out_3), .in1(sub8_unsigned_1_out_3), .in2(mul8_unsigned_1_m),
    .in3(dev8_unsigned_1_q), .in4(mod8_unsigned_1_r), .in5(shifter_8_1_out_4), .in6(shifter_8_2_out_4),
    .in7(shifter_8_3_out_4), .in8(shifter_8_4_out_4), .out(R), .sel(\Код ));  // open: in9, in10, in11, in12, in13, in14, in15, en
endmodule

module convert_straight (
  input  [7:0] in_1,
  output [7:0] out_2
);

  wire [7:0] not_1_out, subtractor_1_out;

  Subtractor subtractor_1 (.a(in_1), .b(8'h1), .out(subtractor_1_out));  // open: bin, bout
  assign not_1_out = ~subtractor_1_out;  // NOT_Gate not_1, 8 bits wide
  Multiplexer #(.width(8)) multiplexer_1 (.in0(in_1), .in1(not_1_out), .out(out_2), .sel(in_1[7]));  // open: en
endmodule

module cmp_float (
  input  [16:0] in_1,
  input  [16:0] in_2,
  output out_3,
  output out_4,
  output out_5,
  output out_6,
  output out_7,
  output out_8
);

  wire and_1_out, and_2_out, and_3_out, and_4_out, and_5_out, and_6_out, isnan_1_r, isnfinity_1_r,
       isnfinity_2_r, not_1_out_2, not_2_out_2, not_3_out_2, not_4_out_2, not_5_out, not_6_out, not_7_out,
       not_8_out, not_9_out, or_1_out, or_2_out, \З_out_3 , \З_out_4 , \З_out_5 , \М_out_3 , \М_out_4 ,
       \М_out_5 , \Ноль_out , \П_out_3 , \П_out_4 , \П_out_5 ;

  NOT not_1 (.in_1(in_1[15:8]), .out_2(not_1_out_2));
  NOT not_2 (.in_1(in_1[7:0]), .out_2(not_2_out_2));
  NOT not_3 (.in_1(in_2[7:0]), .out_2(not_3_out_2));
  NOT not_4 (.in_1(in_2[15:8]), .out_2(not_4_out_2));
  cmp8_unsigned \u_П  (.in_1(in_1[15:8]), .in_2(in_2[15:8]), .out_3(\П_out_3 ), .out_4(\П_out_4 ), .out_5(\П_out_5 ));
  cmp8_unsigned \u_М  (.in_1(in_1[7:0]), .in_2(in_2[7:0]), .out_3(\М_out_3 ), .out_4(\М_out_4 ), .out_5(\М_out_5 ));
  not not_5 (not_5_out, in_1[16]);
  cmp1 \u_З  (.in_1(not_5_out), .in_2(not_6_out), .out_3(\З_out_3 ), .out_4(\З_out_4 ), .out_5(\З_out_5 ));
  not not_6 (not_6_out, in_2[16]);
  and \u_Ноль  (\Ноль_out , not_1_out_2, not_2_out_2, not_3_out_2, not_4_out_2);
  isNan isnan_1 (.M1(in_1[7:0]), .\П1 (in_1[15:8]), .\М2 (in_2[7:0]), .\П2 (in_2[15:8]), .R(isnan_1_r));
  IsnFinity isnfinity_1 (.M1(in_2[7:0]), .\П1 (in_2[15:8]), .R(isnfinity_1_r));
  IsnFinity isnfinity_2 (.M1(in_1[7:0]), .\П1 (in_1[15:8]), .R(isnfinity_2_r));
  not not_7 (not_7_out, isnan_1_r);
  not not_8 (not_8_out, and_1_out);
  and and_1 (and_1_out, isnfinity_1_r, isnfinity_2_r, \З_out_4 );
  and and_2 (and_2_out, \З_out_4 , \П_out_4 );
  and and_3 (and_3_out, \З_out_4 , \П_out_3 , \М_out_4 );
  and and_4 (and_4_out, \З_out_4 , \П_out_5 );
  and and_5 (and_5_out, \З_out_4 , \П_out_3 , \М_out_5 );
  and and_6 (and_6_out, not_8_out, not_7_out, \П_out_3 , \М_out_3 , \З_out_4 );
  not not_9 (not_9_out, out_4);
  or or_1 (or_1_out, \З_out_5 , and_2_out, and_3_out);
  or or_2 (or_2_out, \З_out_3 , and_4_out, and_5_out);
  or or_3 (out_4, \Ноль_out , and_6_out);
  and and_7 (out_5, not_9_out, or_1_out);
  and and_8 (out_7, not_9_out, or_2_out);
  not not_10 (out_3, out_4);
  or or_4 (out_6, out_4, out_7);
  or or_5 (out_8, out_4, out_5);
endmodule

module one (
  input  [7:0] in_1,
  output R
);

  and and_1 (R, in_1[0], in_1[1], in_1[2], in_1[3], in_1[4], in_1[5], in_1[6], in_1[7]);
endmodule

module isNan (
  input  [7:0] M1,
  input  [7:0] \П1 ,
  input  [7:0] \М2 ,
  input  [7:0] \П2 ,
  output R
);

  wire and_1_out, and_2_out, not_1_out_2, not_2_out, not_3_out_2, not_4_out, one_1_r, one_2_r;

  NOT not_1 (.in_1(M1), .out_2(not_1_out_2));
  not not_2 (not_2_out, not_1_out_2);
  one one_1 (.in_1(\П1 ), .R(one_1_r));
  NOT not_3 (.in_1(\М2 ), .out_2(not_3_out_2));
  not not_4 (not_4_out, not_3_out_2);
  one one_2 (.in_1(\П2 ), .R(one_2_r));
  and and_1 (and_1_out, not_2_out, one_1_r);
  or or_1 (R, and_1_out, and_2_out);
  and and_2 (and_2_out, not_4_out, one_2_r);
endmodule

module IsnFinity (
  input  [7:0] M1,
  input  [7:0] \П1 ,
  output R
);

  wire not_1_out_2, one_1_r;

  NOT not_1 (.in_1(M1), .out_2(not_1_out_2));
  one one_1 (.in_1(\П1 ), .R(one_1_r));
  and and_1 (R, not_1_out_2, one_1_r);
endmodule
