// Logisim project registor.circ as structural Verilog
module \rs_тригер  (
  input  R,
  input  S,
  output Q,
  output Q_prime
);

  nor nor_1 (Q, R, Q_prime);
  nor nor_2 (Q_prime, S, Q);
endmodule

module D_latch (
  input  \С ,
  input  D,
  output out_3,
  output out_4
);

  wire and_1_out, and_2_out, not_1_out;

  not not_1 (not_1_out, D);
  and and_1 (and_1_out, \С , not_1_out);
  and and_2 (and_2_out, \С , D);
  \rs_тригер  \rs_тригер_1  (.R(and_1_out), .S(and_2_out), .Q(out_3), .Q_prime(out_4));
endmodule

module D_flip_flop (
  input  in_1,
  input  in_2,
  output out_3,
  output out_4
);

  wire d_latch_2_out_3, not_1_out;

  not not_1 (not_1_out, in_1);
  D_latch d_latch_1 (.D(d_latch_2_out_3), .\С (in_1), .out_3(out_3), .out_4(out_4));
  D_latch d_latch_2 (.D(in_2), .\С (not_1_out), .out_3(d_latch_2_out_3));  // open: out_4
endmodule

module registor (
  input  C,
  input  P,
  input  [7:0] in_3,
  output [7:0] out_4
);

  wire and_1_out;

  D_flip_flop d_flip_flop_1 (.in_2(in_3[1]), .in_1(and_1_out), .out_3(out_4[1]));  // open: out_4
  D_flip_flop d_flip_flop_2 (.in_2(in_3[2]), .in_1(and_1_out), .out_3(out_4[2]));  // open: out_4
  D_flip_flop d_flip_flop_3 (.in_2(in_3[3]), .in_1(and_1_out), .out_3(out_4[3]));  // open: out_4
  D_flip_flop d_flip_flop_4 (.in_2(in_3[4]), .in_1(and_1_out), .out_3(out_4[4]));  // open: out_4
  D_flip_flop d_flip_flop_5 (.in_2(in_3[5]), .in_1(and_1_out), .out_3(out_4[5]));  // open: out_4
  D_flip_flop d_flip_flop_6 (.in_2(in_3[6]), .in_1(and_1_out), .out_3(out_4[6]));  // open: out_4
  D_flip_flop d_flip_flop_7 (.in_2(in_3[7]), .in_1(and_1_out), .out_3(out_4[7]));  // open: out_4
  D_flip_flop d_flip_flop_8 (.in_2(in_3[0]), .in_1(and_1_out), .out_3(out_4[0]));  // open: out_4
  and and_1 (and_1_out, C, P);
endmodule

module \счетчик  (
  input  in_1,
  input  [7:0] in_2,
  output [7:0] out_3
);

  wire adder_1_cout, and_1_out, and_2_out, clock_1_out, not_1_out, not_2_out;
  wire [7:0] adder_1_out, transistor_1_out;

  not not_1 (not_1_out, in_1);
  Transistor #(.width(8)) transistor_1 (.in(in_2), .out(transistor_1_out), .gate(in_1));
  Transistor #(.width(8)) transistor_2 (.in(adder_1_out), .out(transistor_1_out), .gate(not_1_out));
  Register register_1 (.D(transistor_1_out), .Q(out_3), .clk(and_1_out));  // open: en, clr
  and and_1 (and_1_out, not_2_out, clock_1_out);
  Clock clock_1 (.out(clock_1_out));
  Adder adder_1 (.a(8'h1), .b(out_3), .out(adder_1_out), .cout(adder_1_cout));  // open: cin
  and and_2 (and_2_out, adder_1_cout, in_1);
  not not_2 (not_2_out, and_2_out);
endmodule
