// Logisim project мультиплексеры.circ as structural Verilog: 6 circuits, main circuit mux2
module mux2 (
  input  x0,
  input  x1,
  input  C,
  output out_4
);

  wire and_1_out, and_2_out, not_1_out;

  not not_1 (not_1_out, C);
  and and_1 (and_1_out, x0, not_1_out);
  and and_2 (and_2_out, x1, C);
  or or_1 (out_4, and_1_out, and_2_out);
endmodule

module mux4 (
  input  x0,
  input  x1,
  input  x2,
  input  x3,
  input  C1,
  input  C0,
  output out_7
);

  wire mux2_1_out_4, mux2_2_out_4;

  mux2 mux2_1 (.x0(x0), .x1(x1), .C(C0), .out_4(mux2_1_out_4));
  mux2 mux2_2 (.x0(x2), .x1(x3), .C(C0), .out_4(mux2_2_out_4));
  mux2 mux2_3 (.x0(mux2_1_out_4), .x1(mux2_2_out_4), .C(C1), .out_4(out_7));
endmodule

module dmx2 (
  input  x,
  input  C,
  output A0,
  output A1
);

  wire not_1_out;

  not not_1 (not_1_out, C);
  and and_1 (A0, x, not_1_out);
  and and_2 (A1, x, C);
endmodule

module dmx4 (
  input  x,
  input  C1,
  input  C0,
  output A0,
  output A1,
  output A2,
  output A3
);

  wire dmx2_1_a0, dmx2_1_a1;

  dmx2 dmx2_1 (.x(x), .C(C0), .A0(dmx2_1_a0), .A1(dmx2_1_a1));
  dmx2 dmx2_2 (.x(dmx2_1_a0), .C(C1), .A0(A0), .A1(A2));
  dmx2 dmx2_3 (.x(dmx2_1_a1), .C(C1), .A0(A1), .A1(A3));
endmodule

module cd8 (
  input  x0,
  input  x1,
  input  x2,
  input  x3,
  input  x4,
  input  x5,
  input  x6,
  input  x7,
  output y0,
  output y1,
  output y3,
  output G
);

  or or_1 (y0, x1, x3, x5, x7);
  or or_2 (y1, x2, x3, x6, x7);
  or or_3 (y3, x4, x5, x6, x7);
  or or_4 (G, x0, x1, x2, x3, x4, x5, x6, x7);
endmodule

module dc8 (
  input  x0,
  input  x1,
  input  x2,
  output A7,
  output A6,
  output A5,
  output A4,
  output A3,
  output A2,
  output A1,
  output A0
);

  wire not_1_out, not_2_out, not_3_out;

  not not_1 (not_1_out, x0);
  not not_2 (not_2_out, x1);
  not not_3 (not_3_out, x2);
  and and_1 (A7, x0, x1, x2);
  and and_2 (A6, not_1_out, x1, x2);
  and and_3 (A5, x0, not_2_out, x2);
  and and_4 (A4, not_1_out, not_2_out, x2);
  and and_5 (A3, x0, x1, not_3_out);
  and and_6 (A2, not_1_out, x1, not_3_out);
  and and_7 (A1, x0, not_2_out, not_3_out);
  and and_8 (A0, not_2_out, not_1_out, not_3_out);
endmodule
